// Logisim project 4511.circ as structural Verilog: 1 circuit, main circuit 4511
module _4511 (
  input  nBL,
  input  D3,
  input  D2,
  input  D1,
  input  D0,
  input  nLT,
  input  nLE,
  output A,
  output B,
  output C,
  output D,
  output E,
  output F,
  output G
);

  wire d_ff_1_q, d_ff_1_qn, d_ff_2_q, d_ff_2_qn, d_ff_3_q, d_ff_3_qn, d_ff_4_q, d_ff_4_qn, nand_1_out,
       nand_2_out, nand_3_out, nand_4_out, nand_5_out, nand_6_out, nand_7_out, nand_8_out, nand_9_out,
       nand_10_out, nand_11_out, nand_12_out, nand_13_out, nand_14_out, nand_15_out, nand_16_out,
       nand_17_out, nand_18_out, not_1_out, or_1_out;

  D_Flip_Flop d_ff_1 (.clk(nLE), .D(D3), .Q(d_ff_1_q), .Qn(d_ff_1_qn));  // open: preset, en, reset
  D_Flip_Flop d_ff_2 (.clk(nLE), .D(D2), .Q(d_ff_2_q), .Qn(d_ff_2_qn));  // open: preset, en, reset
  D_Flip_Flop d_ff_3 (.clk(nLE), .D(D1), .Q(d_ff_3_q), .Qn(d_ff_3_qn));  // open: preset, en, reset
  D_Flip_Flop d_ff_4 (.clk(nLE), .D(D0), .Q(d_ff_4_q), .Qn(d_ff_4_qn));  // open: preset, en, reset
  nand nand_1 (nand_1_out, d_ff_2_q, d_ff_3_q, d_ff_4_qn);
  nand nand_2 (nand_2_out, d_ff_2_q, d_ff_4_q, d_ff_3_qn);
  nand nand_3 (nand_3_out, d_ff_2_q, d_ff_3_qn, d_ff_4_qn);
  nand nand_4 (nand_4_out, d_ff_2_qn, d_ff_3_q, d_ff_4_qn);
  nand nand_5 (nand_5_out, d_ff_4_q, d_ff_3_qn, d_ff_2_qn);
  not not_1 (not_1_out, nand_6_out);
  nand nand_6 (nand_6_out, nBL, nand_7_out);
  nand nand_7 (nand_7_out, d_ff_1_q, or_1_out);
  or or_1 (or_1_out, d_ff_3_q, d_ff_2_q);
  nand nand_8 (nand_8_out, d_ff_4_q, d_ff_1_qn, d_ff_2_qn, d_ff_3_qn);
  nand nand_9 (nand_9_out, d_ff_3_q, d_ff_2_qn);
  nand nand_10 (nand_10_out, d_ff_2_q, d_ff_3_q, d_ff_4_q);
  nand nand_11 (nand_11_out, d_ff_1_qn, d_ff_2_qn, d_ff_3_qn, d_ff_4_qn);
  nand nand_12 (nand_12_out, nand_3_out, nand_1_out, not_1_out, nand_8_out);
  nand nand_13 (nand_13_out, nand_1_out, nand_2_out, not_1_out);
  nand nand_14 (nand_14_out, nand_4_out, not_1_out);
  nand nand_15 (nand_15_out, nand_5_out, nand_3_out, nand_10_out, not_1_out);
  nand nand_16 (nand_16_out, nand_3_out, not_1_out, d_ff_4_qn);
  nand nand_17 (nand_17_out, nand_9_out, not_1_out, nand_10_out, nand_8_out);
  nand nand_18 (nand_18_out, nand_8_out, not_1_out, nand_10_out, nand_11_out);
  nand nand_19 (A, nand_12_out, nLT);
  nand nand_20 (B, nand_13_out, nLT);
  nand nand_21 (C, nand_14_out, nLT);
  nand nand_22 (D, nand_15_out, nLT);
  nand nand_23 (E, nand_16_out, nLT);
  nand nand_24 (F, nand_17_out, nLT);
  nand nand_25 (G, nand_18_out, nLT);
endmodule
