// Logisim project 74109.circ as structural Verilog: 1 circuit, main circuit 74109
module _74109 (
  input  J,
  input  CP,
  input  K,
  input  S,
  input  R,
  output Q,
  output nQ
);

  wire j_k_ff_1_q, j_k_ff_1_qn, nor_1_out, not_1_out, not_2_out, not_3_out;

  not not_1 (not_1_out, K);
  J_K_Flip_Flop j_k_ff_1 (
    .J(J), .clk(CP), .K(not_1_out), .Q(j_k_ff_1_q), .Qn(j_k_ff_1_qn), .preset(not_2_out), .reset(not_3_out));  // open: en
  not not_2 (not_2_out, S);
  not not_3 (not_3_out, R);
  Multiplexer #(.enable("false")) multiplexer_1 (.in0(j_k_ff_1_q), .in1(1'b1), .out(Q), .sel(nor_1_out));
  Multiplexer #(.enable("false")) multiplexer_2 (.in0(j_k_ff_1_qn), .in1(1'b1), .out(nQ), .sel(nor_1_out));
  nor nor_1 (nor_1_out, S, R);
endmodule
