// Logisim project 74138.circ as structural Verilog: 1 circuit, main circuit 74138
module _74138 (
  input  E3,
  input  E2,
  input  E1,
  input  A0,
  input  A1,
  input  A2,
  output Y0,
  output Y1,
  output Y2,
  output Y3,
  output Y4,
  output Y5,
  output Y6,
  output Y7
);

  wire and_1_out, and_2_out, and_3_out, and_4_out, and_5_out, and_6_out, and_7_out, and_8_out, and_9_out,
       buffer_1_out, not_4_out, not_7_out, not_9_out, not_10_out, not_12_out, not_13_out, not_15_out,
       not_16_out;

  not not_1 (Y0, and_1_out);
  and and_1 (and_1_out, not_16_out, not_16_out, not_13_out, not_10_out, and_4_out);
  not not_2 (Y1, and_2_out);
  and and_2 (and_2_out, not_9_out, not_9_out, not_13_out, not_16_out, and_4_out);
  not not_3 (Y2, and_3_out);
  and and_3 (and_3_out, not_10_out, not_10_out, not_12_out, not_16_out, and_4_out);
  and and_4 (and_4_out, buffer_1_out, not_4_out, not_7_out);
  buf buffer_1 (buffer_1_out, E3);
  not not_4 (not_4_out, E2);
  not not_5 (Y4, and_6_out);
  not not_6 (Y3, and_5_out);
  and and_5 (and_5_out, not_9_out, not_9_out, not_12_out, not_16_out, and_4_out);
  and and_6 (and_6_out, not_10_out, not_10_out, not_13_out, not_15_out, and_4_out);
  not not_7 (not_7_out, E1);
  not not_8 (Y5, and_7_out);
  and and_7 (and_7_out, not_13_out, not_13_out, not_15_out, not_9_out, and_4_out);
  not not_9 (not_9_out, not_10_out);
  not not_10 (not_10_out, A0);
  not not_11 (Y6, and_8_out);
  and and_8 (and_8_out, not_10_out, not_10_out, not_15_out, not_12_out, and_4_out);
  not not_12 (not_12_out, not_13_out);
  not not_13 (not_13_out, A1);
  not not_14 (Y7, and_9_out);
  and and_9 (and_9_out, and_4_out, and_4_out, not_12_out, not_9_out, not_15_out);
  not not_15 (not_15_out, not_16_out);
  not not_16 (not_16_out, A2);
endmodule
