// Logisim project 74147.circ as structural Verilog: 1 circuit, main circuit 74147
module _74147 (
  input  A8,
  input  A7,
  input  A6,
  input  A5,
  input  A4,
  input  A3,
  input  A2,
  input  A1,
  input  A0,
  output Y3,
  output Y2,
  output Y1,
  output Y0
);

  wire and_1_out, and_2_out, and_3_out, and_4_out, and_5_out, and_6_out, and_7_out, and_8_out, and_9_out,
       and_10_out, and_11_out, and_12_out, and_13_out, nor_1_out, not_1_out, not_2_out, not_3_out, not_4_out,
       not_5_out, not_6_out, not_7_out, not_8_out, not_9_out, not_10_out, not_11_out, not_12_out, not_13_out;

  not not_1 (not_1_out, A8);
  nor nor_1 (nor_1_out, not_1_out, not_2_out);
  nor nor_2 (Y3, not_1_out, not_2_out);
  not not_2 (not_2_out, A7);
  not not_3 (not_3_out, A6);
  and and_1 (and_1_out, nor_1_out, not_3_out);
  not not_4 (not_4_out, A5);
  not not_5 (not_5_out, not_4_out);
  and and_2 (and_2_out, nor_1_out, not_4_out);
  and and_3 (and_3_out, nor_1_out, not_6_out);
  nor nor_3 (Y2, and_1_out, and_2_out, and_3_out, and_4_out);
  not not_6 (not_6_out, A4);
  not not_7 (not_7_out, not_6_out);
  and and_4 (and_4_out, nor_1_out, not_8_out);
  and and_5 (and_5_out, nor_1_out, not_3_out);
  not not_8 (not_8_out, A3);
  not not_9 (not_9_out, not_8_out);
  and and_6 (and_6_out, nor_1_out, not_7_out, not_9_out, not_10_out);
  and and_7 (and_7_out, nor_1_out, not_4_out);
  nor nor_4 (Y1, and_5_out, and_7_out, and_6_out, and_8_out);
  not not_10 (not_10_out, A2);
  and and_8 (and_8_out, nor_1_out, not_7_out, not_9_out, not_11_out);
  not not_11 (not_11_out, A1);
  not not_12 (not_12_out, not_11_out);
  and and_9 (and_9_out, nor_1_out, not_3_out);
  and and_10 (and_10_out, not_1_out, not_1_out);
  not not_13 (not_13_out, A0);
  and and_11 (and_11_out, nor_1_out, not_5_out, not_6_out);
  nor nor_5 (Y0, and_10_out, and_9_out, and_11_out, and_12_out, and_13_out);
  and and_12 (and_12_out, nor_1_out, not_5_out, not_9_out, not_10_out);
  and and_13 (and_13_out, nor_1_out, not_5_out, not_9_out, not_12_out, not_13_out);
endmodule
