// Logisim project 74148.circ as structural Verilog: 1 circuit, main circuit 74148
module _74148 (
  input  _0,
  input  _1,
  input  _2,
  input  _3,
  input  _4,
  input  _5,
  input  _6,
  input  _7,
  input  EI,
  output Y0,
  output Y1,
  output Y2,
  output GS,
  output EO
);

  wire not_1_out, not_2_out, not_3_out, not_4_out, not_5_out, not_6_out, not_7_out, not_8_out, not_9_out,
       priority_encoder_1_en_out, priority_encoder_1_gs;
  wire [2:0] not_10_out, priority_encoder_1_out;

  not not_1 (not_1_out, _0);
  not not_2 (not_2_out, _1);
  not not_3 (not_3_out, _2);
  not not_4 (not_4_out, _3);
  not not_5 (not_5_out, _4);
  not not_6 (not_6_out, _5);
  not not_7 (not_7_out, _6);
  not not_8 (not_8_out, _7);
  not not_9 (not_9_out, EI);
  assign not_10_out = ~priority_encoder_1_out;  // NOT_Gate not_10, 3 bits wide
  Priority_Encoder #(.disabled(0)) priority_encoder_1 (
    .in0(not_1_out), .in1(not_2_out), .in2(not_3_out), .in3(not_4_out), .in4(not_5_out), .in5(not_6_out),
    .in6(not_7_out), .in7(not_8_out), .out(priority_encoder_1_out), .en_in(not_9_out),
    .gs(priority_encoder_1_gs), .en_out(priority_encoder_1_en_out));
  Multiplexer #(.width(3), .enable("false")) multiplexer_1 (
    .in0(not_10_out), .in1(3'b111), .out({Y2, Y1, Y0}), .sel(priority_encoder_1_en_out));
  or or_1 (GS, priority_encoder_1_en_out, EI);
  or or_2 (EO, priority_encoder_1_gs, EI);
endmodule
