// Logisim project 74151.circ as structural Verilog: 1 circuit, main circuit 74151
module _74151 (
  input  A7,
  input  A6,
  input  A5,
  input  A4,
  input  A3,
  input  A2,
  input  A1,
  input  A0,
  input  S2,
  input  S1,
  input  S0,
  input  nE,
  output nY,
  output Y
);

  wire and_1_out, and_2_out, and_3_out, and_4_out, and_5_out, and_6_out, and_7_out, and_8_out, buffer_1_out,
       buffer_2_out, buffer_3_out, buffer_4_out, buffer_5_out, buffer_6_out, buffer_7_out, buffer_8_out,
       nor_1_out, not_1_out, not_2_out, not_3_out, not_4_out, not_5_out, not_6_out, not_7_out;

  buf buffer_1 (buffer_1_out, A7);
  buf buffer_2 (buffer_2_out, A6);
  buf buffer_3 (buffer_3_out, A5);
  buf buffer_4 (buffer_4_out, A4);
  buf buffer_5 (buffer_5_out, A3);
  buf buffer_6 (buffer_6_out, A2);
  buf buffer_7 (buffer_7_out, A1);
  buf buffer_8 (buffer_8_out, A0);
  not not_1 (not_1_out, not_3_out);
  not not_2 (not_2_out, not_4_out);
  not not_3 (not_3_out, S1);
  not not_4 (not_4_out, S2);
  not not_5 (not_5_out, not_7_out);
  not not_6 (not_6_out, nE);
  not not_7 (not_7_out, S0);
  and and_1 (and_1_out, not_6_out, not_2_out, not_5_out, not_1_out, buffer_1_out);
  and and_2 (and_2_out, not_6_out, not_7_out, not_2_out, not_1_out, buffer_2_out);
  and and_3 (and_3_out, not_6_out, not_2_out, not_5_out, not_3_out, buffer_3_out);
  and and_4 (and_4_out, not_6_out, not_7_out, not_2_out, not_3_out, buffer_4_out);
  and and_5 (and_5_out, not_6_out, not_5_out, not_1_out, not_4_out, buffer_5_out);
  and and_6 (and_6_out, not_6_out, not_7_out, not_1_out, not_4_out, buffer_6_out);
  and and_7 (and_7_out, not_6_out, not_5_out, not_3_out, not_4_out, buffer_7_out);
  and and_8 (and_8_out, not_6_out, not_7_out, not_3_out, not_4_out, buffer_8_out);
  nor nor_1 (nor_1_out, and_1_out, and_2_out, and_3_out, and_4_out, and_5_out, and_6_out, and_7_out, and_8_out);
  buf buffer_9 (nY, nor_1_out);
  not not_8 (Y, nor_1_out);
endmodule
