// Logisim project 74153.circ as structural Verilog: 1 circuit, main circuit 74153
module _74153 (
  input  a0,
  input  a1,
  input  a2,
  input  a3,
  input  nE1,
  input  b0,
  input  b1,
  input  b2,
  input  b3,
  input  nE2,
  input  S0,
  input  S1,
  output _1Y,
  output _2Y
);

  wire not_1_out, not_2_out;

  Multiplexer #(.select(2), .disabled(0)) multiplexer_1 (
    .in0(a0), .in1(a1), .in2(a2), .in3(a3), .out(_1Y), .sel({S1, S0}), .en(not_1_out));
  not not_1 (not_1_out, nE1);
  Multiplexer #(.select(2), .disabled(0)) multiplexer_2 (
    .in0(b0), .in1(b1), .in2(b2), .in3(b3), .out(_2Y), .sel({S1, S0}), .en(not_2_out));
  not not_2 (not_2_out, nE2);
endmodule
