// Logisim project 74154.circ as structural Verilog: 1 circuit, main circuit 74154
module _74154 (
  input  E0,
  input  E1,
  input  A0,
  input  A1,
  input  A2,
  input  A3,
  output Y0,
  output Y1,
  output Y2,
  output Y3,
  output Y4,
  output Y5,
  output Y6,
  output Y7,
  output Y8,
  output Y9,
  output Y10,
  output Y11,
  output Y12,
  output Y13,
  output Y14,
  output Y15
);

  wire decoder_1_out0, decoder_1_out1, decoder_1_out2, decoder_1_out3, decoder_1_out4, decoder_1_out5,
       decoder_1_out6, decoder_1_out7, decoder_1_out8, decoder_1_out9, decoder_1_out10, decoder_1_out11,
       decoder_1_out12, decoder_1_out13, decoder_1_out14, decoder_1_out15, nor_1_out;
  wire [3:0] buffer_1_out;

  nor nor_1 (nor_1_out, E0, E1);
  not not_1 (Y0, decoder_1_out0);
  not not_2 (Y1, decoder_1_out1);
  not not_3 (Y2, decoder_1_out2);
  not not_4 (Y3, decoder_1_out3);
  not not_5 (Y4, decoder_1_out4);
  not not_6 (Y5, decoder_1_out5);
  not not_7 (Y6, decoder_1_out6);
  not not_8 (Y7, decoder_1_out7);
  not not_9 (Y8, decoder_1_out8);
  not not_10 (Y9, decoder_1_out9);
  not not_11 (Y10, decoder_1_out10);
  not not_12 (Y11, decoder_1_out11);
  not not_13 (Y12, decoder_1_out12);
  not not_14 (Y13, decoder_1_out13);
  not not_15 (Y14, decoder_1_out14);
  not not_16 (Y15, decoder_1_out15);
  Decoder #(.select(4), .disabled(0)) decoder_1 (
    .out0(decoder_1_out0), .out1(decoder_1_out1), .out2(decoder_1_out2), .out3(decoder_1_out3),
    .out4(decoder_1_out4), .out5(decoder_1_out5), .out6(decoder_1_out6), .out7(decoder_1_out7),
    .out8(decoder_1_out8), .out9(decoder_1_out9), .out10(decoder_1_out10), .out11(decoder_1_out11),
    .out12(decoder_1_out12), .out13(decoder_1_out13), .out14(decoder_1_out14), .out15(decoder_1_out15),
    .sel(buffer_1_out), .en(nor_1_out));
  assign buffer_1_out = {A3, A2, A1, A0};  // Buffer buffer_1, 4 bits wide
endmodule
