// Logisim project 74157.circ as structural Verilog: 1 circuit, main circuit 74157
module _74157 (
  input  A1,
  input  B1,
  input  A2,
  input  B2,
  input  A3,
  input  B3,
  input  A4,
  input  B4,
  input  SELECT,
  input  STROBE,
  output Y1,
  output Y2,
  output Y3,
  output Y4
);

  wire not_1_out;

  Multiplexer #(.disabled(0)) multiplexer_1 (.in0(A1), .in1(B1), .out(Y1), .sel(SELECT), .en(not_1_out));
  Multiplexer #(.disabled(0)) multiplexer_2 (.in0(A2), .in1(B2), .out(Y2), .sel(SELECT), .en(not_1_out));
  Multiplexer #(.disabled(0)) multiplexer_3 (.in0(A3), .in1(B3), .out(Y3), .sel(SELECT), .en(not_1_out));
  Multiplexer #(.disabled(0)) multiplexer_4 (.in0(A4), .in1(B4), .out(Y4), .sel(SELECT), .en(not_1_out));
  not not_1 (not_1_out, STROBE);

  // Notes on the sheet:
  //   Y2: pull=down
  //   Y3: pull=down
  //   Y4: pull=down
  //   Y1: pull=down
endmodule
