// Logisim project 74160.circ as structural Verilog: 1 circuit, main circuit 74160
module _74160 (
  input  D0,
  input  D1,
  input  D2,
  input  D3,
  input  CET,
  input  CEP,
  input  nPE,
  input  nMR,
  input  CLK,
  output Q0,
  output Q1,
  output Q2,
  output Q3,
  output TC
);

  wire and_1_out, counter_1_carry, not_1_out, not_2_out;
  wire [3:0] counter_1_q;

  and and_1 (and_1_out, CET, nPE, CEP);
  not not_1 (not_1_out, nPE);
  Counter #(.width(4), .max('h9)) counter_1 (
    .load(not_1_out), .D({D3, D2, D1, D0}), .count(and_1_out), .Q(counter_1_q), .carry(counter_1_carry),
    .clk(CLK), .clr(not_2_out));
  assign {Q3, Q2, Q1, Q0} = counter_1_q;  // Buffer buffer_1, 4 bits wide
  not not_2 (not_2_out, nMR);
  and and_2 (TC, counter_1_carry, CET);
endmodule
