// Logisim project 74165.circ as structural Verilog: 1 circuit, main circuit 74165
module _74165 (
  input  A,
  input  B,
  input  C,
  input  D,
  input  E,
  input  F,
  input  G,
  input  H,
  input  SH_LD,
  input  SER,
  input  CLK_INH,
  input  CLK,
  output QH,
  output nQH,
  output [7:0] test
);

  wire nand_1_out, nand_2_out, nand_3_out, nand_4_out, nand_5_out, nand_6_out, nand_7_out, nand_8_out,
       nand_9_out, nand_10_out, nand_11_out, nand_12_out, nand_13_out, nand_14_out, nand_15_out, nand_16_out,
       nor_1_out, not_1_out, not_2_out, not_3_out, not_4_out, not_5_out, not_6_out, not_7_out, not_8_out,
       not_9_out, not_10_out, not_11_out, not_12_out, not_13_out, not_14_out, not_15_out, not_16_out,
       not_17_out;

  not not_1 (not_1_out, SH_LD);
  nand nand_1 (nand_1_out, not_1_out, A);
  nor nor_1 (nor_1_out, CLK_INH, CLK);
  D_Flip_Flop d_ff_1 (.clk(nor_1_out), .D(SER), .Q(test[0]), .preset(not_3_out), .reset(not_2_out));  // open: Qn, en
  not not_2 (not_2_out, nand_2_out);
  not not_3 (not_3_out, nand_1_out);
  nand nand_2 (nand_2_out, nand_1_out, not_1_out);
  nand nand_3 (nand_3_out, not_1_out, B);
  D_Flip_Flop d_ff_2 (
    .clk(nor_1_out), .D(test[0]), .Q(test[1]), .preset(not_4_out), .reset(not_5_out));  // open: Qn, en
  not not_4 (not_4_out, nand_3_out);
  not not_5 (not_5_out, nand_4_out);
  nand nand_4 (nand_4_out, nand_3_out, not_1_out);
  nand nand_5 (nand_5_out, not_1_out, C);
  not not_6 (not_6_out, nand_5_out);
  not not_7 (not_7_out, nand_6_out);
  nand nand_6 (nand_6_out, nand_5_out, not_1_out);
  nand nand_7 (nand_7_out, not_1_out, D);
  D_Flip_Flop d_ff_3 (
    .clk(nor_1_out), .D(test[1]), .Q(test[2]), .preset(not_6_out), .reset(not_7_out));  // open: Qn, en
  not not_8 (not_8_out, nand_7_out);
  nand nand_8 (nand_8_out, not_1_out, E);
  D_Flip_Flop d_ff_4 (
    .clk(nor_1_out), .D(test[2]), .Q(test[3]), .preset(not_8_out), .reset(not_9_out));  // open: Qn, en
  not not_9 (not_9_out, nand_9_out);
  nand nand_9 (nand_9_out, nand_7_out, not_1_out);
  D_Flip_Flop d_ff_5 (
    .clk(nor_1_out), .D(test[3]), .Q(test[4]), .preset(not_11_out), .reset(not_10_out));  // open: Qn, en
  not not_10 (not_10_out, nand_10_out);
  not not_11 (not_11_out, nand_8_out);
  nand nand_10 (nand_10_out, nand_8_out, not_1_out);
  nand nand_11 (nand_11_out, not_1_out, F);
  D_Flip_Flop d_ff_6 (
    .clk(nor_1_out), .D(test[4]), .Q(test[5]), .preset(not_12_out), .reset(not_13_out));  // open: Qn, en
  not not_12 (not_12_out, nand_11_out);
  not not_13 (not_13_out, nand_12_out);
  nand nand_12 (nand_12_out, nand_11_out, not_1_out);
  nand nand_13 (nand_13_out, not_1_out, G);
  not not_14 (not_14_out, nand_14_out);
  not not_15 (not_15_out, nand_13_out);
  nand nand_14 (nand_14_out, nand_13_out, not_1_out);
  nand nand_15 (nand_15_out, not_1_out, H);
  D_Flip_Flop d_ff_7 (
    .clk(nor_1_out), .D(test[5]), .Q(test[6]), .preset(not_15_out), .reset(not_14_out));  // open: Qn, en
  not not_16 (not_16_out, nand_15_out);
  D_Flip_Flop d_ff_8 (
    .clk(nor_1_out), .D(test[6]), .Q(QH), .Qn(nQH), .preset(not_16_out), .reset(not_17_out));  // open: en
  not not_17 (not_17_out, nand_16_out);
  nand nand_16 (nand_16_out, nand_15_out, not_1_out);

  assign test[7] = QH;
endmodule
