// Logisim project 74173.circ as structural Verilog: 1 circuit, main circuit 74173
module _74173 (
  input  D0,
  input  D1,
  input  D2,
  input  D3,
  input  nE1,
  input  nE2,
  input  CLK,
  input  MR,
  input  nOE1,
  input  nOE2,
  output Q0,
  output Q1,
  output Q2,
  output Q3
);

  wire and_1_out, and_2_out, and_3_out, and_4_out, and_5_out, and_6_out, and_7_out, and_8_out, and_9_out,
       and_10_out, buffer_1_out, buffer_2_out, buffer_3_out, buffer_4_out, buffer_5_out, buffer_6_out,
       buffer_7_out, buffer_8_out, buffer_9_out, buffer_10_out, buffer_11_out, d_ff_1_q, d_ff_1_qn, d_ff_2_q,
       d_ff_2_qn, d_ff_3_q, d_ff_3_qn, d_ff_4_q, d_ff_4_qn, not_1_out, not_2_out, or_1_out, or_2_out,
       or_3_out, or_4_out;

  buf buffer_1 (buffer_1_out, nE1);
  buf buffer_2 (buffer_2_out, nE2);
  buf buffer_3 (buffer_3_out, nOE1);
  buf buffer_4 (buffer_4_out, nOE2);
  and and_1 (and_1_out, ~buffer_1_out, ~buffer_2_out);  // AND_Gate
  buf buffer_5 (buffer_5_out, CLK);
  not not_1 (not_1_out, buffer_5_out);
  buf buffer_6 (buffer_6_out, MR);
  buf buffer_7 (buffer_7_out, buffer_6_out);
  and and_2 (and_2_out, ~buffer_3_out, ~buffer_4_out);  // AND_Gate
  buf buffer_8 (buffer_8_out, D0);
  not not_2 (not_2_out, and_1_out);
  and and_3 (and_3_out, and_1_out, buffer_8_out);
  or or_1 (or_1_out, and_3_out, and_4_out);
  and and_4 (and_4_out, not_2_out, d_ff_1_q);
  D_Flip_Flop #(.trigger("falling")) d_ff_1 (
    .clk(not_1_out), .D(or_1_out), .Q(d_ff_1_q), .Qn(d_ff_1_qn), .reset(buffer_7_out));  // open: preset, en
  assign Q0 = and_2_out ? ~d_ff_1_qn : 1'bz;  // Controlled_Inverter controlled_inverter_1
  buf buffer_9 (buffer_9_out, D1);
  and and_5 (and_5_out, and_1_out, buffer_9_out);
  and and_6 (and_6_out, not_2_out, d_ff_2_q);
  or or_2 (or_2_out, and_5_out, and_6_out);
  and and_7 (and_7_out, and_1_out, buffer_10_out);
  D_Flip_Flop #(.trigger("falling")) d_ff_2 (
    .clk(not_1_out), .D(or_2_out), .Q(d_ff_2_q), .Qn(d_ff_2_qn), .reset(buffer_7_out));  // open: preset, en
  assign Q1 = and_2_out ? ~d_ff_2_qn : 1'bz;  // Controlled_Inverter controlled_inverter_2
  buf buffer_10 (buffer_10_out, D2);
  and and_8 (and_8_out, not_2_out, d_ff_3_q);
  or or_3 (or_3_out, and_7_out, and_8_out);
  D_Flip_Flop #(.trigger("falling")) d_ff_3 (
    .clk(not_1_out), .D(or_3_out), .Q(d_ff_3_q), .Qn(d_ff_3_qn), .reset(buffer_7_out));  // open: preset, en
  assign Q2 = and_2_out ? ~d_ff_3_qn : 1'bz;  // Controlled_Inverter controlled_inverter_3
  buf buffer_11 (buffer_11_out, D3);
  and and_9 (and_9_out, and_1_out, buffer_11_out);
  or or_4 (or_4_out, and_9_out, and_10_out);
  and and_10 (and_10_out, not_2_out, d_ff_4_q);
  D_Flip_Flop #(.trigger("falling")) d_ff_4 (
    .clk(not_1_out), .D(or_4_out), .Q(d_ff_4_q), .Qn(d_ff_4_qn), .reset(buffer_7_out));  // open: preset, en
  assign Q3 = and_2_out ? ~d_ff_4_qn : 1'bz;  // Controlled_Inverter controlled_inverter_4
endmodule
