// Logisim project test 74181.circ as structural Verilog: 1 circuit, main circuit main
module main (
  input  [3:0] S,
  input  [3:0] A,
  input  [3:0] B,
  input  M,
  input  Cn,
  output G,
  output Cn_4,
  output P,
  output A_B,
  output [3:0] F
);

  // _74181 74181_1: pin names not known; wires that end beside it: B[3], A[3], B[2], A[2], B[1], A[1], B[0], A[0], M, Cn, G, Cn_4, P, F[3], F[2], A_B, F[1], F[0]
endmodule
