// Logisim project test 74182.circ as structural Verilog: 1 circuit, main circuit main
module main (
  input  [3:0] S,
  input  Cn,
  input  [7:0] A,
  input  [7:0] B,
  input  M,
  output [1:0] A_B,
  output out_7,
  output [7:0] out_8,
  output out_9
);

  wire n74181_1_g, n74181_1_p, n74181_2_cn_4, n74182_1_cn_x, not_1_out;

  _74181 u_74181_1 (
    .S3(S[3]), .S2(S[2]), .S1(S[1]), .S0(S[0]), .B3(B[3]), .A3(A[3]), .B2(B[2]), .A2(A[2]), .B1(B[1]),
    .A1(A[1]), .B0(B[0]), .A0(A[0]), .M(M), .Cn(not_1_out), .G(n74181_1_g), .P(n74181_1_p), .F3(out_8[3]),
    .F2(out_8[2]), .A_B(A_B[1]), .F1(out_8[1]), .F0(out_8[0]));  // open: Cn_4
  not not_1 (not_1_out, Cn);
  _74181 u_74181_2 (
    .S3(S[3]), .S2(S[2]), .S1(S[1]), .S0(S[0]), .B3(B[7]), .A3(A[7]), .B2(B[6]), .A2(A[6]), .B1(B[5]),
    .A1(A[5]), .B0(B[4]), .A0(A[4]), .M(M), .Cn(n74182_1_cn_x), .Cn_4(n74181_2_cn_4), .F3(out_8[7]),
    .F2(out_8[6]), .A_B(A_B[0]), .F1(out_8[5]), .F0(out_8[4]));  // open: G, P
  _74182 u_74182_1 (
    .G0(n74181_1_g), .P0(n74181_1_p), .Cn(not_1_out), .G1(1'b0), .P1(1'b0), .G2(1'b0), .P2(1'b0), .G3(1'b0),
    .P3(1'b0), .Cn_x(n74182_1_cn_x));  // open: Cn_y, Cn_z, G, P
  and and_1 (out_7, A_B[0], A_B[1]);
  not not_2 (out_9, n74181_2_cn_4);
endmodule
