// Logisim project 74193.circ as structural Verilog: 1 circuit, main circuit 74193
module _74193 (
  input  D0,
  input  D1,
  input  D2,
  input  D3,
  input  pl,
  input  cpu,
  input  cpd,
  input  mr,
  output tcu,
  output tcd,
  output Q0,
  output Q1,
  output Q2,
  output Q3
);

  wire and_1_out, and_2_out, and_3_out, and_4_out, and_5_out, and_6_out, buffer_1_out, buffer_2_out,
       buffer_3_out, buffer_5_out, buffer_7_out, buffer_9_out, nand_1_out, nand_2_out, nand_3_out,
       nand_4_out, nand_5_out, nand_6_out, nand_7_out, nand_8_out, nand_9_out, nand_10_out, nor_1_out,
       nor_2_out, nor_3_out, nor_4_out, not_1_out, not_2_out, not_3_out, not_4_out, not_5_out, not_6_out,
       not_7_out, not_8_out, or_1_out, or_2_out, or_3_out, or_4_out, t_ff_1_q, t_ff_1_qn, t_ff_2_q,
       t_ff_2_qn, t_ff_3_q, t_ff_3_qn, t_ff_4_q, t_ff_4_qn;

  not not_1 (not_1_out, pl);
  not not_2 (not_2_out, cpu);
  buf buffer_1 (buffer_1_out, not_2_out);
  buf buffer_2 (buffer_2_out, not_3_out);
  not not_3 (not_3_out, cpd);
  not not_4 (not_4_out, mr);
  buf buffer_3 (buffer_3_out, D0);
  nand nand_1 (nand_1_out, not_1_out, buffer_3_out);
  not not_5 (not_5_out, nand_1_out);
  nor nor_1 (nor_1_out, buffer_1_out, buffer_2_out);
  or or_1 (or_1_out, ~not_4_out, ~nand_2_out);  // OR_Gate
  nand nand_2 (nand_2_out, nand_1_out, not_1_out);
  T_Flip_Flop t_ff_1 (
    .clk(nor_1_out), .T(nor_1_out), .Q(t_ff_1_q), .Qn(t_ff_1_qn), .preset(not_5_out), .reset(or_1_out));  // open: en
  buf buffer_4 (Q0, t_ff_1_q);
  and and_1 (and_1_out, not_2_out, t_ff_1_q);
  nor nor_2 (nor_2_out, and_1_out, and_2_out);
  and and_2 (and_2_out, t_ff_1_qn, not_3_out);
  buf buffer_5 (buffer_5_out, D1);
  nand nand_3 (nand_3_out, not_1_out, buffer_5_out);
  nand nand_4 (nand_4_out, nand_3_out, not_1_out);
  not not_6 (not_6_out, nand_3_out);
  T_Flip_Flop t_ff_2 (
    .clk(nor_2_out), .T(nor_2_out), .Q(t_ff_2_q), .Qn(t_ff_2_qn), .preset(not_6_out), .reset(or_2_out));  // open: en
  or or_2 (or_2_out, ~not_4_out, ~nand_4_out);  // OR_Gate
  buf buffer_6 (Q1, t_ff_2_q);
  and and_3 (and_3_out, not_2_out, t_ff_1_q, t_ff_2_q);
  and and_4 (and_4_out, t_ff_2_qn, t_ff_1_qn, not_3_out);
  nor nor_3 (nor_3_out, and_3_out, and_4_out);
  buf buffer_7 (buffer_7_out, D2);
  nand nand_5 (nand_5_out, not_1_out, buffer_7_out);
  nand nand_6 (nand_6_out, nand_5_out, not_1_out);
  not not_7 (not_7_out, nand_5_out);
  T_Flip_Flop t_ff_3 (
    .clk(nor_3_out), .T(nor_3_out), .Q(t_ff_3_q), .Qn(t_ff_3_qn), .preset(not_7_out), .reset(or_3_out));  // open: en
  or or_3 (or_3_out, ~not_4_out, ~nand_6_out);  // OR_Gate
  buf buffer_8 (Q2, t_ff_3_q);
  and and_5 (and_5_out, t_ff_2_q, not_2_out, t_ff_1_q, t_ff_3_q);
  nor nor_4 (nor_4_out, and_5_out, and_6_out);
  and and_6 (and_6_out, t_ff_3_qn, t_ff_2_qn, t_ff_1_qn, not_3_out);
  buf buffer_9 (buffer_9_out, D3);
  nand nand_7 (nand_7_out, not_1_out, buffer_9_out);
  nand nand_8 (nand_8_out, nand_7_out, not_1_out);
  not not_8 (not_8_out, nand_7_out);
  T_Flip_Flop t_ff_4 (
    .clk(nor_4_out), .T(nor_4_out), .Q(t_ff_4_q), .Qn(t_ff_4_qn), .preset(not_8_out), .reset(or_4_out));  // open: en
  or or_4 (or_4_out, ~not_4_out, ~nand_8_out);  // OR_Gate
  buf buffer_10 (Q3, t_ff_4_q);
  nand nand_9 (nand_9_out, t_ff_3_q, not_2_out, t_ff_4_q, t_ff_2_q, t_ff_1_q);
  nand nand_10 (nand_10_out, t_ff_1_qn, t_ff_4_qn, t_ff_3_qn, t_ff_2_qn, not_3_out);
  buf buffer_11 (tcu, nand_9_out);
  buf buffer_12 (tcd, nand_10_out);
endmodule
