// Logisim project 74244.circ as structural Verilog: 1 circuit, main circuit 74244
module _74244 (
  input  in_1,
  input  in_2,
  input  in_3,
  input  in_4,
  input  in_5,
  input  in_6,
  input  in_7,
  input  in_8,
  input  in_9,
  input  in_10,
  output out_11,
  output out_12,
  output out_13,
  output out_14,
  output out_15,
  output out_16,
  output out_17,
  output out_18
);

  wire not_1_out, not_2_out;

  not not_1 (not_1_out, in_10);
  assign out_11 = not_2_out ? in_1 : 1'bz;  // Controlled_Buffer controlled_buffer_1
  assign out_12 = not_2_out ? in_2 : 1'bz;  // Controlled_Buffer controlled_buffer_2
  assign out_13 = not_2_out ? in_3 : 1'bz;  // Controlled_Buffer controlled_buffer_3
  assign out_14 = not_2_out ? in_4 : 1'bz;  // Controlled_Buffer controlled_buffer_4
  assign out_15 = not_1_out ? in_5 : 1'bz;  // Controlled_Buffer controlled_buffer_5
  assign out_16 = not_1_out ? in_6 : 1'bz;  // Controlled_Buffer controlled_buffer_6
  assign out_17 = not_1_out ? in_7 : 1'bz;  // Controlled_Buffer controlled_buffer_7
  assign out_18 = not_1_out ? in_8 : 1'bz;  // Controlled_Buffer controlled_buffer_8
  not not_2 (not_2_out, in_9);
endmodule
