// Logisim project 74273.circ as structural Verilog: 1 circuit, main circuit 74273
module _74273 (
  input  D0,
  input  D1,
  input  D2,
  input  D3,
  input  D4,
  input  D5,
  input  D6,
  input  D7,
  input  nCLEAR,
  input  CLK,
  output Q0,
  output Q1,
  output Q2,
  output Q3,
  output Q4,
  output Q5,
  output Q6,
  output Q7
);

  wire not_1_out;

  not not_1 (not_1_out, nCLEAR);
  Register register_1 (
    .D({D7, D6, D5, D4, D3, D2, D1, D0}), .Q({Q7, Q6, Q5, Q4, Q3, Q2, Q1, Q0}), .clk(CLK), .clr(not_1_out));  // open: en
endmodule
