// Logisim project 74299.circ as structural Verilog: 1 circuit, main circuit 74299
module _74299 (
  input  DSR,
  input  S0,
  input  S1,
  input  CP,
  input  nOE1,
  input  nOE2,
  input  [7:0] in,
  input  DSL,
  input  nMR,
  output [7:0] test,
  output Q0,
  output [7:0] out,
  output Q7
);

  wire and_1_out, and_2_out, and_3_out, and_4_out, and_5_out, and_6_out, and_7_out, and_8_out, and_9_out,
       and_10_out, and_11_out, and_12_out, and_13_out, and_14_out, and_15_out, and_16_out, and_17_out,
       and_18_out, and_19_out, and_20_out, and_21_out, and_22_out, and_23_out, and_24_out, and_25_out,
       and_26_out, and_27_out, and_28_out, and_29_out, and_30_out, and_31_out, and_32_out, buffer_1_out,
       buffer_2_out, buffer_3_out, buffer_6_out, buffer_7_out, buffer_8_out, buffer_9_out, buffer_10_out,
       buffer_11_out, buffer_12_out, buffer_13_out, nand_1_out, nand_2_out, not_1_out, not_2_out, not_3_out,
       not_4_out, not_5_out, not_6_out, not_7_out, or_1_out, or_2_out, or_3_out, or_4_out, or_5_out,
       or_6_out, or_7_out, or_8_out;

  nand nand_1 (nand_1_out, S0, S1);
  buf buffer_1 (buffer_1_out, DSR);
  buf buffer_2 (buffer_2_out, S0);
  not not_1 (not_1_out, buffer_2_out);
  not not_2 (not_2_out, buffer_3_out);
  buf buffer_3 (buffer_3_out, S1);
  not not_3 (not_3_out, CP);
  buf buffer_4 (Q0, test[0]);
  nand nand_2 (nand_2_out, nand_1_out, ~nOE1, ~nOE2);  // NAND_Gate
  not not_4 (not_4_out, not_1_out);
  not not_5 (not_5_out, not_2_out);
  buf buffer_5 (Q7, test[7]);
  not not_6 (not_6_out, nMR);
  and and_1 (and_1_out, buffer_1_out, not_4_out, not_2_out);
  and and_2 (and_2_out, not_5_out, not_1_out, test[1]);
  and and_3 (and_3_out, not_5_out, not_4_out, buffer_6_out);
  and and_4 (and_4_out, not_2_out, not_1_out, test[0]);
  and and_5 (and_5_out, test[0], not_4_out, not_2_out);
  and and_6 (and_6_out, not_5_out, not_1_out, test[2]);
  and and_7 (and_7_out, not_5_out, not_4_out, buffer_7_out);
  and and_8 (and_8_out, not_2_out, not_1_out, test[1]);
  and and_9 (and_9_out, test[1], not_4_out, not_2_out);
  and and_10 (and_10_out, not_5_out, not_1_out, test[3]);
  and and_11 (and_11_out, not_5_out, not_4_out, buffer_8_out);
  and and_12 (and_12_out, not_2_out, not_1_out, test[2]);
  and and_13 (and_13_out, test[2], not_4_out, not_2_out);
  and and_14 (and_14_out, not_5_out, not_1_out, test[4]);
  and and_15 (and_15_out, not_5_out, not_4_out, buffer_9_out);
  and and_16 (and_16_out, not_2_out, not_1_out, test[3]);
  and and_17 (and_17_out, test[3], not_4_out, not_2_out);
  and and_18 (and_18_out, not_5_out, not_1_out, test[5]);
  and and_19 (and_19_out, not_5_out, not_4_out, buffer_10_out);
  and and_20 (and_20_out, not_2_out, not_1_out, test[4]);
  and and_21 (and_21_out, test[4], not_4_out, not_2_out);
  and and_22 (and_22_out, not_5_out, not_1_out, test[6]);
  and and_23 (and_23_out, not_5_out, not_4_out, buffer_11_out);
  and and_24 (and_24_out, not_2_out, not_1_out, test[5]);
  and and_25 (and_25_out, test[5], not_4_out, not_2_out);
  and and_26 (and_26_out, not_5_out, not_1_out, test[7]);
  and and_27 (and_27_out, not_5_out, not_4_out, buffer_12_out);
  and and_28 (and_28_out, not_2_out, not_1_out, test[6]);
  and and_29 (and_29_out, test[6], not_4_out, not_2_out);
  and and_30 (and_30_out, not_5_out, not_1_out, DSL);
  and and_31 (and_31_out, not_5_out, not_4_out, buffer_13_out);
  and and_32 (and_32_out, not_2_out, not_1_out, test[7]);
  or or_1 (or_1_out, and_1_out, and_2_out, and_3_out, and_4_out);
  or or_2 (or_2_out, and_5_out, and_6_out, and_7_out, and_8_out);
  or or_3 (or_3_out, and_9_out, and_10_out, and_11_out, and_12_out);
  or or_4 (or_4_out, and_13_out, and_14_out, and_15_out, and_16_out);
  or or_5 (or_5_out, and_17_out, and_18_out, and_19_out, and_20_out);
  or or_6 (or_6_out, and_21_out, and_22_out, and_23_out, and_24_out);
  or or_7 (or_7_out, and_25_out, and_26_out, and_27_out, and_28_out);
  or or_8 (or_8_out, and_29_out, and_30_out, and_31_out, and_32_out);
  buf buffer_6 (buffer_6_out, in[0]);
  assign out[0] = not_7_out ? test[0] : 1'bz;  // Controlled_Buffer controlled_buffer_1
  D_Flip_Flop #(.trigger("falling")) d_ff_1 (
    .clk(not_3_out), .D(or_1_out), .Q(test[0]), .reset(not_6_out));  // open: Qn, preset, en
  not not_7 (not_7_out, nand_2_out);
  buf buffer_7 (buffer_7_out, in[1]);
  assign out[1] = not_7_out ? test[1] : 1'bz;  // Controlled_Buffer controlled_buffer_2
  D_Flip_Flop #(.trigger("falling")) d_ff_2 (
    .clk(not_3_out), .D(or_2_out), .Q(test[1]), .reset(not_6_out));  // open: Qn, preset, en
  buf buffer_8 (buffer_8_out, in[2]);
  assign out[2] = not_7_out ? test[2] : 1'bz;  // Controlled_Buffer controlled_buffer_3
  D_Flip_Flop #(.trigger("falling")) d_ff_3 (
    .clk(not_3_out), .D(or_3_out), .Q(test[2]), .reset(not_6_out));  // open: Qn, preset, en
  buf buffer_9 (buffer_9_out, in[3]);
  assign out[3] = not_7_out ? test[3] : 1'bz;  // Controlled_Buffer controlled_buffer_4
  D_Flip_Flop #(.trigger("falling")) d_ff_4 (
    .clk(not_3_out), .D(or_4_out), .Q(test[3]), .reset(not_6_out));  // open: Qn, preset, en
  buf buffer_10 (buffer_10_out, in[4]);
  assign out[4] = not_7_out ? test[4] : 1'bz;  // Controlled_Buffer controlled_buffer_5
  D_Flip_Flop #(.trigger("falling")) d_ff_5 (
    .clk(not_3_out), .D(or_5_out), .Q(test[4]), .reset(not_6_out));  // open: Qn, preset, en
  buf buffer_11 (buffer_11_out, in[5]);
  assign out[5] = not_7_out ? test[5] : 1'bz;  // Controlled_Buffer controlled_buffer_6
  D_Flip_Flop #(.trigger("falling")) d_ff_6 (
    .clk(not_3_out), .D(or_6_out), .Q(test[5]), .reset(not_6_out));  // open: Qn, preset, en
  buf buffer_12 (buffer_12_out, in[6]);
  D_Flip_Flop #(.trigger("falling")) d_ff_7 (
    .clk(not_3_out), .D(or_7_out), .Q(test[6]), .reset(not_6_out));  // open: Qn, preset, en
  assign out[6] = not_7_out ? test[6] : 1'bz;  // Controlled_Buffer controlled_buffer_7
  buf buffer_13 (buffer_13_out, in[7]);
  assign out[7] = not_7_out ? test[7] : 1'bz;  // Controlled_Buffer controlled_buffer_8
  D_Flip_Flop #(.trigger("falling")) d_ff_8 (
    .clk(not_3_out), .D(or_8_out), .Q(test[7]), .reset(not_6_out));  // open: Qn, preset, en
endmodule
