// Logisim project 74385.circ as structural Verilog: 1 circuit, main circuit 74385
module _74385 (
  input  CLK,
  input  A,
  input  B,
  input  S_A,
  input  CLR,
  output Q
);

  wire and_1_out, and_2_out, and_3_out, d_ff_2_qn, nand_1_out, nand_2_out, nor_1_out, not_1_out, not_2_out,
       not_3_out, not_4_out, not_5_out, not_6_out, not_7_out, not_8_out, not_9_out, not_10_out, not_11_out,
       not_12_out, xnor_1_out, xnor_2_out, xnor_3_out;

  not not_1 (not_1_out, CLK);
  not not_2 (not_2_out, A);
  not not_3 (not_3_out, B);
  not not_4 (not_4_out, S_A);
  not not_5 (not_5_out, CLR);
  xnor xnor_1 (xnor_1_out, not_3_out, not_4_out);
  not not_6 (not_6_out, not_5_out);
  xnor xnor_2 (xnor_2_out, not_2_out, d_ff_2_qn);
  and and_1 (and_1_out, not_2_out, xnor_1_out);
  and and_2 (and_2_out, not_2_out, d_ff_2_qn);
  and and_3 (and_3_out, xnor_1_out, d_ff_2_qn);
  nand nand_1 (nand_1_out, ~not_4_out, not_5_out);  // NAND_Gate
  nand nand_2 (nand_2_out, not_4_out, not_5_out);
  xnor xnor_3 (xnor_3_out, xnor_2_out, xnor_1_out);
  nor nor_1 (nor_1_out, and_1_out, and_2_out, and_3_out);
  not not_7 (not_7_out, not_1_out);
  D_Flip_Flop d_ff_1 (.clk(not_7_out), .D(not_8_out), .Q(Q), .reset(not_9_out));  // open: Qn, preset, en
  not not_8 (not_8_out, xnor_3_out);
  not not_9 (not_9_out, not_6_out);
  not not_10 (not_10_out, not_1_out);
  D_Flip_Flop d_ff_2 (
    .clk(not_10_out), .D(nor_1_out), .Qn(d_ff_2_qn), .preset(not_11_out), .reset(not_12_out));  // open: Q, en
  not not_11 (not_11_out, nand_1_out);
  not not_12 (not_12_out, nand_2_out);
endmodule
