// Logisim project 7442.circ as structural Verilog: 1 circuit, main circuit 7442
module _7442 (
  input  A0,
  input  A1,
  input  A2,
  input  A3,
  output Y0,
  output Y1,
  output Y2,
  output Y3,
  output Y4,
  output Y5,
  output Y6,
  output Y7,
  output Y8,
  output Y9
);

  wire nand_1_out, nand_2_out, nand_3_out, nand_4_out, nand_5_out, nand_6_out, nand_7_out, not_1_out,
       not_2_out, not_3_out, not_4_out, not_5_out, not_6_out, not_7_out, not_8_out;

  not not_1 (not_1_out, A0);
  not not_2 (not_2_out, A1);
  not not_3 (not_3_out, A2);
  not not_4 (not_4_out, A3);
  not not_5 (not_5_out, not_1_out);
  not not_6 (not_6_out, not_2_out);
  not not_7 (not_7_out, not_3_out);
  not not_8 (not_8_out, not_4_out);
  nand nand_1 (nand_1_out, not_1_out, not_2_out);
  nand nand_2 (nand_2_out, not_5_out, not_2_out);
  nand nand_3 (nand_3_out, not_1_out, not_6_out);
  nand nand_4 (nand_4_out, not_5_out, not_6_out);
  nand nand_5 (nand_5_out, not_3_out, not_4_out);
  nand nand_6 (nand_6_out, not_7_out, not_4_out);
  nand nand_7 (nand_7_out, not_3_out, not_8_out);
  nand nand_8 (Y0, ~nand_1_out, ~nand_5_out);  // NAND_Gate
  nand nand_9 (Y1, ~nand_2_out, ~nand_5_out);  // NAND_Gate
  nand nand_10 (Y2, ~nand_3_out, ~nand_5_out);  // NAND_Gate
  nand nand_11 (Y3, ~nand_4_out, ~nand_5_out);  // NAND_Gate
  nand nand_12 (Y4, ~nand_1_out, ~nand_6_out);  // NAND_Gate
  nand nand_13 (Y5, ~nand_2_out, ~nand_6_out);  // NAND_Gate
  nand nand_14 (Y6, ~nand_3_out, ~nand_6_out);  // NAND_Gate
  nand nand_15 (Y7, ~nand_4_out, ~nand_6_out);  // NAND_Gate
  nand nand_16 (Y8, ~nand_1_out, ~nand_7_out);  // NAND_Gate
  nand nand_17 (Y9, ~nand_2_out, ~nand_7_out);  // NAND_Gate
endmodule
