// Logisim project 7442v2.circ as structural Verilog: 1 circuit, main circuit 7442
module _7442 (
  input  A0,
  input  A1,
  input  A2,
  input  A3,
  output Y0,
  output Y1,
  output Y2,
  output Y3,
  output Y4,
  output Y5,
  output Y6,
  output Y7,
  output Y8,
  output Y9
);

  wire decoder_1_out0, decoder_1_out1, decoder_1_out2, decoder_1_out3, decoder_1_out4, decoder_1_out5,
       decoder_1_out6, decoder_1_out7, decoder_1_out8, decoder_1_out9;

  not not_1 (Y0, decoder_1_out0);
  not not_2 (Y1, decoder_1_out1);
  not not_3 (Y2, decoder_1_out2);
  not not_4 (Y3, decoder_1_out3);
  not not_5 (Y4, decoder_1_out4);
  not not_6 (Y5, decoder_1_out5);
  not not_7 (Y6, decoder_1_out6);
  not not_8 (Y7, decoder_1_out7);
  not not_9 (Y8, decoder_1_out8);
  not not_10 (Y9, decoder_1_out9);
  Decoder #(.select(4), .enable("false")) decoder_1 (
    .out0(decoder_1_out0), .out1(decoder_1_out1), .out2(decoder_1_out2), .out3(decoder_1_out3),
    .out4(decoder_1_out4), .out5(decoder_1_out5), .out6(decoder_1_out6), .out7(decoder_1_out7),
    .out8(decoder_1_out8), .out9(decoder_1_out9), .sel({A3, A2, A1, A0}));  // open: out10, out11, out12, out13, out14, out15
endmodule
