// Logisim project 7451.circ as structural Verilog: 1 circuit, main circuit 7451
module _7451 (
  input  in_1,
  input  in_2,
  input  in_3,
  input  in_4,
  input  in_5,
  input  in_6,
  output out_7
);

  wire and_1_out, and_2_out;

  and and_1 (and_1_out, in_1, in_2, in_3);
  and and_2 (and_2_out, in_4, in_5, in_6);
  nor nor_1 (out_7, and_1_out, and_2_out);
endmodule
