// Logisim project 74670.circ as structural Verilog: 1 circuit, main circuit 74670
module _74670 (
  input  Gr,
  input  Ra,
  input  Rb,
  input  [3:0] D,
  input  Gw,
  input  Wa,
  input  Wb,
  output [3:0] Q,
  output [15:0] test
);

  wire decoder_1_out0, decoder_1_out1, decoder_1_out2, decoder_1_out3, not_1_out, not_2_out;

  not not_1 (not_1_out, Gw);
  Decoder #(.select(2), .disabled(0), .enable("false")) decoder_1 (
    .out0(decoder_1_out0), .out1(decoder_1_out1), .out2(decoder_1_out2), .out3(decoder_1_out3), .sel({Wb, Wa}));
  Register #(.width(4), .trigger("high")) register_1 (
    .D(D), .en(not_1_out), .Q(test[3:0]), .clk(decoder_1_out0));  // open: clr
  Register #(.width(4), .trigger("high")) register_2 (
    .D(D), .en(not_1_out), .Q(test[7:4]), .clk(decoder_1_out1));  // open: clr
  Register #(.width(4), .trigger("high")) register_3 (
    .D(D), .en(not_1_out), .Q(test[11:8]), .clk(decoder_1_out2));  // open: clr
  not not_2 (not_2_out, Gr);
  Multiplexer #(.select(2), .width(4)) multiplexer_1 (
    .in0(test[3:0]), .in1(test[7:4]), .in2(test[11:8]), .in3(test[15:12]), .out(Q), .sel({Rb, Ra}),
    .en(not_2_out));
  Register #(.width(4), .trigger("high")) register_4 (
    .D(D), .en(not_1_out), .Q(test[15:12]), .clk(decoder_1_out3));  // open: clr
endmodule
