// Logisim project 74688.circ as structural Verilog: 1 circuit, main circuit 74688
module _74688 (
  input  [7:0] P,
  input  [7:0] Q,
  input  nE,
  output P_Q
);

  wire not_1_out;
  wire [7:0] xnor_1_out;

  assign xnor_1_out = ~(~P ^ ~Q);  // XNOR_Gate xnor_1, 8 bits wide
  not not_1 (not_1_out, nE);
  nand nand_1 (P_Q, xnor_1_out[0], xnor_1_out[1], xnor_1_out[2], xnor_1_out[3], xnor_1_out[4], xnor_1_out[5], xnor_1_out[6], xnor_1_out[7], not_1_out);
endmodule
