// Logisim project 7474.circ as structural Verilog: 1 circuit, main circuit 7474
module _7474 (
  input  CP,
  input  D,
  input  nSD,
  input  nRD,
  output Q,
  output nQ
);

  wire d_ff_1_q, d_ff_1_qn, nor_1_out, not_1_out, not_2_out;

  not not_1 (not_1_out, nSD);
  not not_2 (not_2_out, nRD);
  D_Flip_Flop d_ff_1 (
    .clk(CP), .D(D), .Q(d_ff_1_q), .Qn(d_ff_1_qn), .preset(not_1_out), .reset(not_2_out));  // open: en
  nor nor_1 (nor_1_out, nSD, nRD);
  Multiplexer #(.enable("false")) multiplexer_1 (.in0(d_ff_1_q), .in1(1'b1), .out(Q), .sel(nor_1_out));
  Multiplexer #(.enable("false")) multiplexer_2 (.in0(d_ff_1_qn), .in1(1'b1), .out(nQ), .sel(nor_1_out));
endmodule
