// Logisim project 7476.circ as structural Verilog: 1 circuit, main circuit 7476
module _7476 (
  input  J,
  input  CK,
  input  K,
  input  nRD,
  input  nSD,
  output Q,
  output nQ
);

  wire j_k_ff_1_q, j_k_ff_1_qn, nor_1_out, not_1_out, not_2_out;

  J_K_Flip_Flop #(.trigger("falling")) j_k_ff_1 (
    .J(J), .clk(CK), .K(K), .Q(j_k_ff_1_q), .Qn(j_k_ff_1_qn), .preset(not_1_out), .reset(not_2_out));  // open: en
  not not_1 (not_1_out, nSD);
  not not_2 (not_2_out, nRD);
  Multiplexer #(.enable("false")) multiplexer_1 (.in0(j_k_ff_1_q), .in1(1'b1), .out(Q), .sel(nor_1_out));
  Multiplexer #(.enable("false")) multiplexer_2 (.in0(j_k_ff_1_qn), .in1(1'b1), .out(nQ), .sel(nor_1_out));
  nor nor_1 (nor_1_out, nSD, nRD);
endmodule
