// Logisim project 74x_library.circ as structural Verilog: 22 circuits, main circuit 74160
module _7474 (
  input  CP,
  input  D,
  input  SD,
  input  RD,
  output Q,
  output Qi
);

  wire d_ff_1_q, d_ff_1_qn, nor_1_out, not_1_out, not_2_out;

  not not_1 (not_1_out, SD);
  not not_2 (not_2_out, RD);
  D_Flip_Flop d_ff_1 (
    .clk(CP), .D(D), .Q(d_ff_1_q), .Qn(d_ff_1_qn), .preset(not_1_out), .reset(not_2_out));  // open: en
  nor nor_1 (nor_1_out, SD, RD);
  Multiplexer #(.enable("false")) multiplexer_1 (.in0(d_ff_1_q), .in1(1'b1), .out(Q), .sel(nor_1_out));
  Multiplexer #(.enable("false")) multiplexer_2 (.in0(d_ff_1_qn), .in1(1'b1), .out(Qi), .sel(nor_1_out));
endmodule

module _7476 (
  input  J,
  input  CP,
  input  K,
  input  RD,
  input  SD,
  output Q,
  output Qi
);

  wire j_k_ff_1_q, j_k_ff_1_qn, nor_1_out, not_1_out, not_2_out;

  J_K_Flip_Flop #(.trigger("falling")) j_k_ff_1 (
    .J(J), .clk(CP), .K(K), .Q(j_k_ff_1_q), .Qn(j_k_ff_1_qn), .preset(not_2_out), .reset(not_1_out));  // open: en
  not not_1 (not_1_out, RD);
  not not_2 (not_2_out, SD);
  Multiplexer #(.enable("false")) multiplexer_1 (.in0(j_k_ff_1_q), .in1(1'b1), .out(Q), .sel(nor_1_out));
  Multiplexer #(.enable("false")) multiplexer_2 (.in0(j_k_ff_1_qn), .in1(1'b1), .out(Qi), .sel(nor_1_out));
  nor nor_1 (nor_1_out, SD, RD);
endmodule

module _74109 (
  input  J,
  input  CP,
  input  K,
  input  S,
  input  R,
  output Q,
  output nQ
);

  wire j_k_ff_1_q, j_k_ff_1_qn, nor_1_out, not_1_out, not_2_out, not_3_out;

  J_K_Flip_Flop j_k_ff_1 (
    .J(J), .clk(CP), .K(not_1_out), .Q(j_k_ff_1_q), .Qn(j_k_ff_1_qn), .preset(not_2_out), .reset(not_3_out));  // open: en
  not not_1 (not_1_out, K);
  not not_2 (not_2_out, S);
  not not_3 (not_3_out, R);
  nor nor_1 (nor_1_out, S, R);
  Multiplexer #(.enable("false")) multiplexer_1 (.in0(j_k_ff_1_q), .in1(1'b1), .out(Q), .sel(nor_1_out));
  Multiplexer #(.enable("false")) multiplexer_2 (.in0(j_k_ff_1_qn), .in1(1'b1), .out(nQ), .sel(nor_1_out));
endmodule

module _74138 (
  input  E3,
  input  iE2,
  input  iE1,
  input  A0,
  input  A1,
  input  A2,
  output Y0,
  output Y1,
  output Y2,
  output Y3,
  output Y4,
  output Y5,
  output Y6,
  output Y7
);

  wire and_1_out, and_2_out, and_3_out, and_4_out, and_5_out, and_6_out, and_7_out, and_8_out, and_9_out,
       buffer_1_out, not_5_out, not_6_out, not_10_out, not_11_out, not_12_out, not_13_out, not_15_out,
       not_16_out;

  not not_1 (Y0, and_2_out);
  not not_2 (Y1, and_1_out);
  and and_1 (and_1_out, not_11_out, not_11_out, not_13_out, not_16_out, and_5_out);
  and and_2 (and_2_out, not_16_out, not_16_out, not_13_out, not_12_out, and_5_out);
  not not_3 (Y2, and_3_out);
  and and_3 (and_3_out, not_12_out, not_12_out, not_10_out, not_16_out, and_5_out);
  buf buffer_1 (buffer_1_out, E3);
  not not_4 (Y3, and_4_out);
  and and_4 (and_4_out, not_11_out, not_11_out, not_10_out, not_16_out, and_5_out);
  and and_5 (and_5_out, buffer_1_out, not_5_out, not_6_out);
  not not_5 (not_5_out, iE2);
  not not_6 (not_6_out, iE1);
  not not_7 (Y4, and_7_out);
  not not_8 (Y5, and_6_out);
  and and_6 (and_6_out, not_13_out, not_13_out, not_15_out, not_11_out, and_5_out);
  and and_7 (and_7_out, not_12_out, not_12_out, not_13_out, not_15_out, and_5_out);
  not not_9 (Y6, and_8_out);
  and and_8 (and_8_out, not_12_out, not_12_out, not_15_out, not_10_out, and_5_out);
  not not_10 (not_10_out, not_13_out);
  not not_11 (not_11_out, not_12_out);
  not not_12 (not_12_out, A0);
  not not_13 (not_13_out, A1);
  not not_14 (Y7, and_9_out);
  and and_9 (and_9_out, and_5_out, and_5_out, not_10_out, not_11_out, not_15_out);
  not not_15 (not_15_out, not_16_out);
  not not_16 (not_16_out, A2);
endmodule

module _74154 (
  input  iE0,
  input  iE1,
  input  A0,
  input  A1,
  input  A2,
  input  A3,
  output Y0,
  output Y1,
  output Y2,
  output Y3,
  output Y4,
  output Y5,
  output Y6,
  output Y7,
  output Y8,
  output Y9,
  output Y10,
  output Y11,
  output Y12,
  output Y13,
  output Y14,
  output Y15
);

  wire decoder_1_out0, decoder_1_out1, decoder_1_out2, decoder_1_out3, decoder_1_out4, decoder_1_out5,
       decoder_1_out6, decoder_1_out7, decoder_1_out8, decoder_1_out9, decoder_1_out10, decoder_1_out11,
       decoder_1_out12, decoder_1_out13, decoder_1_out14, decoder_1_out15, nor_1_out;
  wire [3:0] buffer_1_out;

  nor nor_1 (nor_1_out, iE0, iE1);
  not not_1 (Y0, decoder_1_out0);
  not not_2 (Y1, decoder_1_out1);
  not not_3 (Y2, decoder_1_out2);
  not not_4 (Y3, decoder_1_out3);
  not not_5 (Y4, decoder_1_out4);
  not not_6 (Y5, decoder_1_out5);
  not not_7 (Y6, decoder_1_out6);
  not not_8 (Y7, decoder_1_out7);
  not not_9 (Y8, decoder_1_out8);
  not not_10 (Y9, decoder_1_out9);
  not not_11 (Y10, decoder_1_out10);
  not not_12 (Y11, decoder_1_out11);
  not not_13 (Y12, decoder_1_out12);
  not not_14 (Y13, decoder_1_out13);
  not not_15 (Y14, decoder_1_out14);
  not not_16 (Y15, decoder_1_out15);
  Decoder #(.select(4), .disabled(0)) decoder_1 (
    .out0(decoder_1_out0), .out1(decoder_1_out1), .out2(decoder_1_out2), .out3(decoder_1_out3),
    .out4(decoder_1_out4), .out5(decoder_1_out5), .out6(decoder_1_out6), .out7(decoder_1_out7),
    .out8(decoder_1_out8), .out9(decoder_1_out9), .out10(decoder_1_out10), .out11(decoder_1_out11),
    .out12(decoder_1_out12), .out13(decoder_1_out13), .out14(decoder_1_out14), .out15(decoder_1_out15),
    .sel(buffer_1_out), .en(nor_1_out));
  assign buffer_1_out = {A3, A2, A1, A0};  // Buffer buffer_1, 4 bits wide
endmodule

module _74160 (
  input  D0,
  input  D1,
  input  D2,
  input  D3,
  input  CET,
  input  CEP,
  input  PE,
  input  MR,
  input  CP,
  output Q0,
  output Q1,
  output Q2,
  output Q3,
  output TC
);

  wire and_1_out, and_2_out, and_3_out, and_4_out, and_5_out, and_6_out, and_7_out, and_8_out, and_9_out,
       buffer_1_out, buffer_2_out, buffer_3_out, buffer_4_out, buffer_5_out, buffer_6_out, d_ff_1_q,
       d_ff_1_qn, d_ff_2_qn, d_ff_3_qn, d_ff_4_q, d_ff_4_qn, nand_1_out, nand_2_out, nor_1_out, nor_2_out,
       nor_3_out, nor_4_out, nor_5_out, nor_6_out, not_1_out, not_2_out, not_3_out, not_4_out, not_5_out,
       or_1_out, or_2_out, or_3_out, or_4_out, or_5_out, xnor_1_out, xnor_2_out, xnor_3_out;

  buf buffer_1 (buffer_1_out, CET);
  buf buffer_2 (buffer_2_out, CEP);
  not not_1 (not_1_out, not_2_out);
  not not_2 (not_2_out, PE);
  not not_3 (not_3_out, MR);
  not not_4 (not_4_out, CP);
  buf buffer_3 (buffer_3_out, D0);
  nand nand_1 (nand_1_out, buffer_1_out, buffer_2_out);
  and and_1 (and_1_out, buffer_3_out, not_2_out);
  not not_5 (not_5_out, nand_1_out);
  xnor xnor_1 (xnor_1_out, not_5_out, d_ff_1_qn);
  and and_2 (and_2_out, xnor_1_out, not_1_out);
  or or_1 (or_1_out, and_1_out, and_2_out);
  D_Flip_Flop #(.trigger("falling")) d_ff_1 (
    .clk(not_4_out), .D(or_1_out), .Q(d_ff_1_q), .Qn(d_ff_1_qn), .reset(not_3_out));  // open: preset, en
  buf buffer_4 (buffer_4_out, D1);
  nor nor_1 (nor_1_out, d_ff_1_qn, nand_1_out, d_ff_4_q);
  xnor xnor_2 (xnor_2_out, nor_1_out, d_ff_2_qn);
  and and_3 (and_3_out, buffer_4_out, not_2_out);
  and and_4 (and_4_out, xnor_2_out, not_1_out);
  or or_2 (or_2_out, and_3_out, and_4_out);
  not not_6 (Q0, d_ff_1_qn);
  buf buffer_5 (buffer_5_out, D2);
  D_Flip_Flop #(.trigger("falling")) d_ff_2 (
    .clk(not_4_out), .D(or_2_out), .Qn(d_ff_2_qn), .reset(not_3_out));  // open: Q, preset, en
  not not_7 (Q1, d_ff_2_qn);
  nor nor_2 (nor_2_out, nand_1_out, d_ff_2_qn, d_ff_1_qn);
  xnor xnor_3 (xnor_3_out, nor_2_out, d_ff_3_qn);
  and and_5 (and_5_out, buffer_5_out, not_2_out);
  and and_6 (and_6_out, xnor_3_out, not_1_out);
  or or_3 (or_3_out, and_5_out, and_6_out);
  buf buffer_6 (buffer_6_out, D3);
  nor nor_3 (nor_3_out, nand_1_out, d_ff_3_qn, d_ff_2_qn, d_ff_1_qn);
  and and_7 (and_7_out, buffer_6_out, not_2_out);
  or or_4 (or_4_out, and_7_out, and_9_out);
  D_Flip_Flop #(.trigger("falling")) d_ff_3 (
    .clk(not_4_out), .D(or_3_out), .Qn(d_ff_3_qn), .reset(not_3_out));  // open: Q, preset, en
  not not_8 (Q2, d_ff_3_qn);
  nor nor_4 (nor_4_out, nand_1_out, nor_6_out);
  nor nor_5 (nor_5_out, d_ff_4_qn, nor_4_out);
  and and_8 (and_8_out, nor_3_out, d_ff_4_qn);
  or or_5 (or_5_out, and_8_out, nor_5_out);
  and and_9 (and_9_out, not_1_out, or_5_out);
  D_Flip_Flop #(.trigger("falling")) d_ff_4 (
    .clk(not_4_out), .D(or_4_out), .Q(d_ff_4_q), .Qn(d_ff_4_qn), .reset(not_3_out));  // open: preset, en
  not not_9 (Q3, d_ff_4_qn);
  nor nor_6 (nor_6_out, d_ff_1_q, d_ff_4_qn);
  nand nand_2 (nand_2_out, d_ff_4_q, d_ff_3_qn, d_ff_2_qn, d_ff_1_q, buffer_1_out);
  not not_10 (TC, nand_2_out);
endmodule

module _74161 (
  input  D0,
  input  D1,
  input  D2,
  input  D3,
  input  CET,
  input  CEP,
  input  PE,
  input  MR,
  input  CP,
  output Q0,
  output Q1,
  output Q2,
  output Q3,
  output TC
);

  wire and_1_out, and_2_out, and_3_out, and_4_out, and_5_out, and_6_out, and_7_out, and_8_out, and_9_out,
       buffer_1_out, buffer_2_out, d_ff_1_q, d_ff_1_qn, d_ff_2_q, d_ff_2_qn, d_ff_3_q, d_ff_3_qn, d_ff_4_q,
       d_ff_4_qn, nand_1_out, nand_2_out, nor_1_out, nor_2_out, nor_3_out, nor_4_out, not_1_out, not_2_out,
       not_3_out, not_4_out, not_5_out, or_1_out, or_2_out, or_3_out, or_4_out, or_5_out, xnor_1_out,
       xnor_2_out, xnor_3_out;

  buf buffer_1 (buffer_1_out, CET);
  buf buffer_2 (buffer_2_out, CEP);
  not not_1 (not_1_out, PE);
  not not_2 (not_2_out, not_1_out);
  not not_3 (not_3_out, MR);
  not not_4 (not_4_out, CP);
  nand nand_1 (nand_1_out, buffer_1_out, buffer_2_out);
  and and_1 (and_1_out, D0, not_1_out);
  not not_5 (not_5_out, nand_1_out);
  xnor xnor_1 (xnor_1_out, not_5_out, d_ff_1_qn);
  and and_2 (and_2_out, xnor_1_out, not_2_out);
  or or_1 (or_1_out, and_1_out, and_2_out);
  D_Flip_Flop #(.trigger("falling")) d_ff_1 (
    .clk(not_4_out), .D(or_1_out), .Q(d_ff_1_q), .Qn(d_ff_1_qn), .reset(not_3_out));  // open: preset, en
  nor nor_1 (nor_1_out, nand_1_out, d_ff_1_qn);
  xnor xnor_2 (xnor_2_out, nor_1_out, d_ff_2_qn);
  and and_3 (and_3_out, D1, not_1_out);
  and and_4 (and_4_out, xnor_2_out, not_2_out);
  or or_2 (or_2_out, and_3_out, and_4_out);
  not not_6 (Q0, d_ff_1_qn);
  D_Flip_Flop #(.trigger("falling")) d_ff_2 (
    .clk(not_4_out), .D(or_2_out), .Q(d_ff_2_q), .Qn(d_ff_2_qn), .reset(not_3_out));  // open: preset, en
  not not_7 (Q1, d_ff_2_qn);
  nor nor_2 (nor_2_out, nand_1_out, d_ff_2_qn, d_ff_1_qn);
  xnor xnor_3 (xnor_3_out, nor_2_out, d_ff_3_qn);
  and and_5 (and_5_out, xnor_3_out, not_2_out);
  and and_6 (and_6_out, D2, not_1_out);
  or or_3 (or_3_out, and_6_out, and_5_out);
  nor nor_3 (nor_3_out, nand_1_out, d_ff_3_qn, d_ff_2_qn, d_ff_1_qn);
  and and_7 (and_7_out, D3, not_1_out);
  or or_4 (or_4_out, and_7_out, and_9_out);
  D_Flip_Flop #(.trigger("falling")) d_ff_3 (
    .clk(not_4_out), .D(or_3_out), .Q(d_ff_3_q), .Qn(d_ff_3_qn), .reset(not_3_out));  // open: preset, en
  not not_8 (Q2, d_ff_3_qn);
  and and_8 (and_8_out, nor_3_out, d_ff_4_qn);
  nor nor_4 (nor_4_out, nor_3_out, d_ff_4_qn);
  or or_5 (or_5_out, and_8_out, nor_4_out);
  and and_9 (and_9_out, not_2_out, or_5_out);
  D_Flip_Flop #(.trigger("falling")) d_ff_4 (
    .clk(not_4_out), .D(or_4_out), .Q(d_ff_4_q), .Qn(d_ff_4_qn), .reset(not_3_out));  // open: preset, en
  not not_9 (Q3, d_ff_4_qn);
  nand nand_2 (nand_2_out, d_ff_4_q, d_ff_3_q, d_ff_2_q, d_ff_1_q, buffer_1_out);
  not not_10 (TC, nand_2_out);
endmodule

module _74163 (
  input  D0,
  input  D1,
  input  D2,
  input  D3,
  input  CET,
  input  CEP,
  input  PE,
  input  MR,
  input  CP,
  output Q0,
  output Q1,
  output Q2,
  output Q3,
  output TC
);

  wire and_1_out, and_2_out, and_3_out, and_4_out, and_5_out, and_6_out, and_7_out, and_8_out, and_9_out,
       buffer_1_out, buffer_2_out, buffer_3_out, d_ff_1_q, d_ff_1_qn, d_ff_2_q, d_ff_2_qn, d_ff_3_q,
       d_ff_3_qn, d_ff_4_q, d_ff_4_qn, nand_1_out, nand_2_out, nor_1_out, nor_2_out, nor_3_out, nor_4_out,
       nor_5_out, nor_6_out, not_1_out, not_2_out, not_3_out, or_1_out, or_2_out, or_3_out, or_4_out,
       or_5_out, xnor_1_out, xnor_2_out, xnor_3_out;

  buf buffer_1 (buffer_1_out, PE);
  buf buffer_2 (buffer_2_out, CET);
  buf buffer_3 (buffer_3_out, CEP);
  nor nor_1 (nor_1_out, buffer_1_out, not_1_out);
  not not_1 (not_1_out, MR);
  not not_2 (not_2_out, CP);
  nand nand_1 (nand_1_out, buffer_2_out, buffer_3_out);
  nor nor_2 (nor_2_out, nor_1_out, not_1_out);
  and and_1 (and_1_out, D0, nor_1_out);
  not not_3 (not_3_out, nand_1_out);
  xnor xnor_1 (xnor_1_out, not_3_out, d_ff_1_qn);
  and and_2 (and_2_out, xnor_1_out, nor_2_out);
  or or_1 (or_1_out, and_1_out, and_2_out);
  D_Flip_Flop #(.trigger("falling")) d_ff_1 (
    .clk(not_2_out), .D(or_1_out), .Q(d_ff_1_q), .Qn(d_ff_1_qn));  // open: preset, en, reset
  nor nor_3 (nor_3_out, nand_1_out, d_ff_1_qn);
  xnor xnor_2 (xnor_2_out, nor_3_out, d_ff_2_qn);
  and and_3 (and_3_out, xnor_2_out, nor_2_out);
  and and_4 (and_4_out, D1, nor_1_out);
  or or_2 (or_2_out, and_4_out, and_3_out);
  not not_4 (Q0, d_ff_1_qn);
  D_Flip_Flop #(.trigger("falling")) d_ff_2 (
    .clk(not_2_out), .D(or_2_out), .Q(d_ff_2_q), .Qn(d_ff_2_qn));  // open: preset, en, reset
  not not_5 (Q1, d_ff_2_qn);
  nor nor_4 (nor_4_out, nand_1_out, d_ff_2_qn, d_ff_1_qn);
  xnor xnor_3 (xnor_3_out, nor_4_out, d_ff_3_qn);
  and and_5 (and_5_out, D2, nor_1_out);
  and and_6 (and_6_out, xnor_3_out, nor_2_out);
  or or_3 (or_3_out, and_5_out, and_6_out);
  nor nor_5 (nor_5_out, nand_1_out, d_ff_3_qn, d_ff_2_qn, d_ff_1_qn);
  and and_7 (and_7_out, D3, nor_1_out);
  or or_4 (or_4_out, and_7_out, and_9_out);
  D_Flip_Flop #(.trigger("falling")) d_ff_3 (
    .clk(not_2_out), .D(or_3_out), .Q(d_ff_3_q), .Qn(d_ff_3_qn));  // open: preset, en, reset
  not not_6 (Q2, d_ff_3_qn);
  and and_8 (and_8_out, nor_5_out, d_ff_4_qn);
  nor nor_6 (nor_6_out, nor_5_out, d_ff_4_qn);
  or or_5 (or_5_out, and_8_out, nor_6_out);
  and and_9 (and_9_out, nor_2_out, or_5_out);
  D_Flip_Flop #(.trigger("falling")) d_ff_4 (
    .clk(not_2_out), .D(or_4_out), .Q(d_ff_4_q), .Qn(d_ff_4_qn));  // open: preset, en, reset
  not not_7 (Q3, d_ff_4_qn);
  nand nand_2 (nand_2_out, d_ff_4_q, d_ff_3_q, d_ff_2_q, d_ff_1_q, buffer_2_out);
  not not_8 (TC, nand_2_out);
endmodule

module _74669 (
  input  D0,
  input  D1,
  input  D2,
  input  D3,
  input  PE,
  input  CEP,
  input  CET,
  input  UD,
  input  CP,
  output TC,
  output Q0,
  output Q1,
  output Q2,
  output Q3
);

  wire and_1_out, and_2_out, and_3_out, and_4_out, and_5_out, and_6_out, and_7_out, and_8_out, and_9_out,
       and_10_out, and_11_out, and_12_out, and_13_out, and_14_out, and_15_out, and_16_out, and_17_out,
       and_18_out, and_19_out, and_20_out, and_21_out, d_ff_1_qn, d_ff_2_qn, d_ff_3_qn, d_ff_4_qn,
       nand_1_out, nand_2_out, nand_3_out, nand_4_out, nand_5_out, nand_6_out, not_1_out, not_2_out,
       not_3_out, not_4_out, not_5_out, not_6_out, or_1_out, or_2_out, or_3_out, or_4_out;

  and and_1 (and_1_out, ~CEP, ~CET);  // AND_Gate
  not not_1 (not_1_out, UD);
  not not_2 (not_2_out, PE);
  not not_3 (not_3_out, not_2_out);
  not not_4 (not_4_out, CET);
  not not_5 (not_5_out, not_1_out);
  not not_6 (not_6_out, CP);
  and and_2 (and_2_out, not_3_out, ~and_1_out, Q0);  // AND_Gate
  and and_3 (and_3_out, not_2_out, D0);
  and and_4 (and_4_out, and_1_out, not_3_out, ~Q0);  // AND_Gate
  or or_1 (or_1_out, and_2_out, and_3_out, and_4_out);
  D_Flip_Flop #(.trigger("falling")) d_ff_1 (
    .clk(not_6_out), .D(or_1_out), .Q(Q0), .Qn(d_ff_1_qn));  // open: preset, en, reset
  nand nand_1 (nand_1_out, d_ff_1_qn, and_1_out);
  and and_5 (and_5_out, nand_1_out, not_3_out, Q1, not_1_out);
  and and_6 (and_6_out, not_2_out, D1);
  and and_7 (and_7_out, ~Q1, not_1_out, not_3_out, d_ff_1_qn, and_1_out);  // AND_Gate
  or or_2 (or_2_out, and_5_out, and_7_out, and_6_out, and_8_out, and_9_out);
  nand nand_2 (nand_2_out, Q0, and_1_out);
  and and_8 (and_8_out, Q1, nand_2_out, not_3_out, not_5_out);
  D_Flip_Flop #(.trigger("falling")) d_ff_2 (
    .clk(not_6_out), .D(or_2_out), .Q(Q1), .Qn(d_ff_2_qn));  // open: preset, en, reset
  and and_9 (and_9_out, ~Q1, not_3_out, not_5_out, and_1_out, Q0);  // AND_Gate
  nand nand_3 (nand_3_out, Q1, Q0, and_1_out);
  and and_10 (and_10_out, nand_3_out, not_3_out, Q2, not_5_out);
  and and_11 (and_11_out, not_5_out, not_3_out, Q1, Q0, and_1_out, ~Q2);  // AND_Gate
  and and_12 (and_12_out, not_2_out, D2);
  nand nand_4 (nand_4_out, d_ff_2_qn, and_1_out, d_ff_1_qn);
  and and_13 (and_13_out, Q2, nand_4_out, not_3_out, not_1_out);
  or or_3 (or_3_out, and_10_out, and_11_out, and_12_out, and_13_out, and_14_out);
  D_Flip_Flop #(.trigger("falling")) d_ff_3 (
    .clk(not_6_out), .D(or_3_out), .Q(Q2), .Qn(d_ff_3_qn));  // open: preset, en, reset
  and and_14 (and_14_out, ~Q2, not_1_out, and_1_out, not_3_out, d_ff_2_qn, d_ff_1_qn);  // AND_Gate
  nand nand_5 (nand_5_out, d_ff_3_qn, d_ff_2_qn, d_ff_1_qn, and_1_out);
  and and_15 (and_15_out, nand_5_out, Q3, not_3_out, not_1_out);
  and and_16 (and_16_out, not_1_out, not_3_out, and_1_out, d_ff_3_qn, d_ff_2_qn, d_ff_1_qn, ~Q3);  // AND_Gate
  and and_17 (and_17_out, not_2_out, D3);
  nand nand_6 (nand_6_out, Q2, Q1, Q0, and_1_out);
  or or_4 (or_4_out, and_15_out, and_16_out, and_17_out, and_18_out, and_19_out);
  and and_18 (and_18_out, Q3, nand_6_out, not_3_out, not_5_out);
  D_Flip_Flop #(.trigger("falling")) d_ff_4 (
    .clk(not_6_out), .D(or_4_out), .Q(Q3), .Qn(d_ff_4_qn));  // open: preset, en, reset
  and and_19 (and_19_out, ~Q3, not_3_out, not_5_out, and_1_out, Q2, Q1, Q0);  // AND_Gate
  and and_20 (and_20_out, not_1_out, d_ff_1_qn, d_ff_2_qn, d_ff_3_qn, d_ff_4_qn, not_4_out);
  and and_21 (and_21_out, not_4_out, not_5_out, Q0, Q1, Q2, Q3);
  nor nor_1 (TC, and_20_out, and_21_out);
endmodule

module _74193 (
  input  D0,
  input  D1,
  input  D2,
  input  D3,
  input  pl,
  input  cpu,
  input  cpd,
  input  mr,
  output tcu,
  output tcd,
  output Q0,
  output Q1,
  output Q2,
  output Q3
);

  wire and_1_out, and_2_out, and_3_out, and_4_out, and_5_out, and_6_out, buffer_1_out, buffer_2_out,
       buffer_3_out, buffer_5_out, buffer_7_out, buffer_9_out, nand_1_out, nand_2_out, nand_3_out,
       nand_4_out, nand_5_out, nand_6_out, nand_7_out, nand_8_out, nand_9_out, nand_10_out, nor_1_out,
       nor_2_out, nor_3_out, nor_4_out, not_1_out, not_2_out, not_3_out, not_4_out, not_5_out, not_6_out,
       not_7_out, not_8_out, or_1_out, or_2_out, or_3_out, or_4_out, t_ff_1_q, t_ff_1_qn, t_ff_2_q,
       t_ff_2_qn, t_ff_3_q, t_ff_3_qn, t_ff_4_q, t_ff_4_qn;

  not not_1 (not_1_out, pl);
  not not_2 (not_2_out, cpu);
  buf buffer_1 (buffer_1_out, not_2_out);
  buf buffer_2 (buffer_2_out, not_3_out);
  not not_3 (not_3_out, cpd);
  not not_4 (not_4_out, mr);
  buf buffer_3 (buffer_3_out, D0);
  nand nand_1 (nand_1_out, not_1_out, buffer_3_out);
  not not_5 (not_5_out, nand_1_out);
  nor nor_1 (nor_1_out, buffer_1_out, buffer_2_out);
  or or_1 (or_1_out, ~not_4_out, ~nand_2_out);  // OR_Gate
  nand nand_2 (nand_2_out, nand_1_out, not_1_out);
  T_Flip_Flop t_ff_1 (
    .clk(nor_1_out), .T(nor_1_out), .Q(t_ff_1_q), .Qn(t_ff_1_qn), .preset(not_5_out), .reset(or_1_out));  // open: en
  buf buffer_4 (Q0, t_ff_1_q);
  and and_1 (and_1_out, not_2_out, t_ff_1_q);
  nor nor_2 (nor_2_out, and_1_out, and_2_out);
  and and_2 (and_2_out, t_ff_1_qn, not_3_out);
  buf buffer_5 (buffer_5_out, D1);
  nand nand_3 (nand_3_out, not_1_out, buffer_5_out);
  nand nand_4 (nand_4_out, nand_3_out, not_1_out);
  not not_6 (not_6_out, nand_3_out);
  T_Flip_Flop t_ff_2 (
    .clk(nor_2_out), .T(nor_2_out), .Q(t_ff_2_q), .Qn(t_ff_2_qn), .preset(not_6_out), .reset(or_2_out));  // open: en
  or or_2 (or_2_out, ~not_4_out, ~nand_4_out);  // OR_Gate
  buf buffer_6 (Q1, t_ff_2_q);
  and and_3 (and_3_out, not_2_out, t_ff_1_q, t_ff_2_q);
  and and_4 (and_4_out, t_ff_2_qn, t_ff_1_qn, not_3_out);
  nor nor_3 (nor_3_out, and_3_out, and_4_out);
  buf buffer_7 (buffer_7_out, D2);
  nand nand_5 (nand_5_out, nand_6_out, not_1_out);
  nand nand_6 (nand_6_out, not_1_out, buffer_7_out);
  not not_7 (not_7_out, nand_6_out);
  T_Flip_Flop t_ff_3 (
    .clk(nor_3_out), .T(nor_3_out), .Q(t_ff_3_q), .Qn(t_ff_3_qn), .preset(not_7_out), .reset(or_3_out));  // open: en
  or or_3 (or_3_out, ~not_4_out, ~nand_5_out);  // OR_Gate
  buf buffer_8 (Q2, t_ff_3_q);
  and and_5 (and_5_out, t_ff_2_q, not_2_out, t_ff_1_q, t_ff_3_q);
  nor nor_4 (nor_4_out, and_5_out, and_6_out);
  and and_6 (and_6_out, t_ff_3_qn, t_ff_2_qn, t_ff_1_qn, not_3_out);
  buf buffer_9 (buffer_9_out, D3);
  nand nand_7 (nand_7_out, nand_8_out, not_1_out);
  nand nand_8 (nand_8_out, not_1_out, buffer_9_out);
  not not_8 (not_8_out, nand_8_out);
  T_Flip_Flop t_ff_4 (
    .clk(nor_4_out), .T(nor_4_out), .Q(t_ff_4_q), .Qn(t_ff_4_qn), .preset(not_8_out), .reset(or_4_out));  // open: en
  or or_4 (or_4_out, ~not_4_out, ~nand_7_out);  // OR_Gate
  buf buffer_10 (Q3, t_ff_4_q);
  nand nand_9 (nand_9_out, t_ff_3_q, not_2_out, t_ff_4_q, t_ff_2_q, t_ff_1_q);
  nand nand_10 (nand_10_out, t_ff_1_qn, t_ff_4_qn, t_ff_3_qn, t_ff_2_qn, not_3_out);
  buf buffer_11 (tcu, nand_9_out);
  buf buffer_12 (tcd, nand_10_out);
endmodule

module _74164 (
  input  DSA,
  input  DSB,
  input  CP,
  input  MR,
  output Q0,
  output Q1,
  output Q2,
  output Q3,
  output Q4,
  output Q5,
  output Q6,
  output Q7
);

  wire and_1_out, buffer_1_out, not_1_out;

  and and_1 (and_1_out, DSA, DSB);
  buf buffer_1 (buffer_1_out, CP);
  not not_1 (not_1_out, MR);
  D_Flip_Flop d_ff_1 (.clk(buffer_1_out), .D(and_1_out), .Q(Q0), .reset(not_1_out));  // open: Qn, preset, en
  D_Flip_Flop d_ff_2 (.clk(buffer_1_out), .D(Q0), .Q(Q1), .reset(not_1_out));  // open: Qn, preset, en
  D_Flip_Flop d_ff_3 (.clk(buffer_1_out), .D(Q1), .Q(Q2), .reset(not_1_out));  // open: Qn, preset, en
  D_Flip_Flop d_ff_4 (.clk(buffer_1_out), .D(Q2), .Q(Q3), .reset(not_1_out));  // open: Qn, preset, en
  D_Flip_Flop d_ff_5 (.clk(buffer_1_out), .D(Q3), .Q(Q4), .reset(not_1_out));  // open: Qn, preset, en
  D_Flip_Flop d_ff_6 (.clk(buffer_1_out), .D(Q4), .Q(Q5), .reset(not_1_out));  // open: Qn, preset, en
  D_Flip_Flop d_ff_7 (.clk(buffer_1_out), .D(Q5), .Q(Q6), .reset(not_1_out));  // open: Qn, preset, en
  D_Flip_Flop d_ff_8 (.clk(buffer_1_out), .D(Q6), .Q(Q7), .reset(not_1_out));  // open: Qn, preset, en
endmodule

module _74165 (
  input  D0,
  input  D1,
  input  D2,
  input  D3,
  input  D4,
  input  D5,
  input  D6,
  input  D7,
  input  PL,
  input  DS,
  input  CE,
  input  CP,
  output Q7,
  output iQ7,
  output [7:0] test
);

  wire nand_1_out, nand_2_out, nand_3_out, nand_4_out, nand_5_out, nand_6_out, nand_7_out, nand_8_out,
       nand_9_out, nand_10_out, nand_11_out, nand_12_out, nand_13_out, nand_14_out, nand_15_out, nand_16_out,
       nor_1_out, not_1_out, not_2_out, not_3_out, not_4_out, not_5_out, not_6_out, not_7_out, not_8_out,
       not_9_out, not_10_out, not_11_out, not_12_out, not_13_out, not_14_out, not_15_out, not_16_out,
       not_17_out;

  not not_1 (not_1_out, PL);
  nand nand_1 (nand_1_out, not_1_out, D0);
  nor nor_1 (nor_1_out, CE, CP);
  D_Flip_Flop d_ff_1 (.clk(nor_1_out), .D(DS), .Q(test[0]), .preset(not_3_out), .reset(not_2_out));  // open: Qn, en
  not not_2 (not_2_out, nand_2_out);
  not not_3 (not_3_out, nand_1_out);
  nand nand_2 (nand_2_out, nand_1_out, not_1_out);
  nand nand_3 (nand_3_out, not_1_out, D1);
  D_Flip_Flop d_ff_2 (
    .clk(nor_1_out), .D(test[0]), .Q(test[1]), .preset(not_5_out), .reset(not_4_out));  // open: Qn, en
  not not_4 (not_4_out, nand_4_out);
  not not_5 (not_5_out, nand_3_out);
  nand nand_4 (nand_4_out, nand_3_out, not_1_out);
  nand nand_5 (nand_5_out, not_1_out, D2);
  not not_6 (not_6_out, nand_5_out);
  not not_7 (not_7_out, nand_6_out);
  nand nand_6 (nand_6_out, nand_5_out, not_1_out);
  nand nand_7 (nand_7_out, not_1_out, D3);
  D_Flip_Flop d_ff_3 (
    .clk(nor_1_out), .D(test[1]), .Q(test[2]), .preset(not_6_out), .reset(not_7_out));  // open: Qn, en
  not not_8 (not_8_out, nand_7_out);
  nand nand_8 (nand_8_out, not_1_out, D4);
  D_Flip_Flop d_ff_4 (
    .clk(nor_1_out), .D(test[2]), .Q(test[3]), .preset(not_8_out), .reset(not_9_out));  // open: Qn, en
  not not_9 (not_9_out, nand_9_out);
  nand nand_9 (nand_9_out, nand_7_out, not_1_out);
  D_Flip_Flop d_ff_5 (
    .clk(nor_1_out), .D(test[3]), .Q(test[4]), .preset(not_10_out), .reset(not_11_out));  // open: Qn, en
  not not_10 (not_10_out, nand_8_out);
  not not_11 (not_11_out, nand_10_out);
  nand nand_10 (nand_10_out, nand_8_out, not_1_out);
  nand nand_11 (nand_11_out, not_1_out, D5);
  D_Flip_Flop d_ff_6 (
    .clk(nor_1_out), .D(test[4]), .Q(test[5]), .preset(not_12_out), .reset(not_13_out));  // open: Qn, en
  not not_12 (not_12_out, nand_11_out);
  not not_13 (not_13_out, nand_12_out);
  nand nand_12 (nand_12_out, nand_11_out, not_1_out);
  nand nand_13 (nand_13_out, not_1_out, D6);
  not not_14 (not_14_out, nand_14_out);
  not not_15 (not_15_out, nand_13_out);
  nand nand_14 (nand_14_out, nand_13_out, not_1_out);
  nand nand_15 (nand_15_out, not_1_out, D7);
  D_Flip_Flop d_ff_7 (
    .clk(nor_1_out), .D(test[5]), .Q(test[6]), .preset(not_15_out), .reset(not_14_out));  // open: Qn, en
  not not_16 (not_16_out, nand_15_out);
  D_Flip_Flop d_ff_8 (
    .clk(nor_1_out), .D(test[6]), .Q(Q7), .Qn(iQ7), .preset(not_16_out), .reset(not_17_out));  // open: en
  not not_17 (not_17_out, nand_16_out);
  nand nand_16 (nand_16_out, nand_15_out, not_1_out);

  assign test[7] = Q7;
endmodule

module _74166 (
  input  D0,
  input  D1,
  input  D2,
  input  D3,
  input  D4,
  input  D5,
  input  D6,
  input  D7,
  input  PE,
  input  DS,
  input  CP,
  input  CE,
  input  MR,
  output Q7,
  output [7:0] test
);

  wire and_1_out, and_2_out, and_3_out, and_4_out, and_5_out, and_6_out, and_7_out, and_8_out, and_9_out,
       and_10_out, and_11_out, and_12_out, and_13_out, and_14_out, and_15_out, and_16_out, buffer_1_out,
       buffer_2_out, buffer_3_out, buffer_4_out, buffer_5_out, buffer_6_out, buffer_7_out, buffer_8_out,
       buffer_9_out, buffer_10_out, buffer_11_out, nor_1_out, nor_2_out, nor_3_out, nor_4_out, nor_5_out,
       nor_6_out, nor_7_out, nor_8_out, nor_9_out, not_1_out, not_2_out, not_3_out, not_4_out, not_5_out,
       not_6_out, not_7_out, not_8_out, not_9_out, not_10_out, not_11_out, s_r_ff_8_q;

  not not_1 (not_1_out, PE);
  not not_2 (not_2_out, not_1_out);
  buf buffer_1 (buffer_1_out, DS);
  buf buffer_2 (buffer_2_out, CP);
  buf buffer_3 (buffer_3_out, CE);
  not not_3 (not_3_out, MR);
  buf buffer_4 (buffer_4_out, D0);
  and and_1 (and_1_out, not_1_out, buffer_4_out);
  and and_2 (and_2_out, buffer_1_out, not_2_out);
  nor nor_1 (nor_1_out, and_2_out, and_1_out);
  not not_4 (not_4_out, nor_1_out);
  nor nor_2 (nor_2_out, buffer_2_out, buffer_3_out);
  and and_3 (and_3_out, test[7], not_2_out);
  nor nor_3 (nor_3_out, and_3_out, and_4_out);
  not not_5 (not_5_out, nor_3_out);
  S_R_Flip_Flop #(.trigger("falling")) s_r_ff_1 (
    .S(not_4_out), .clk(nor_2_out), .R(nor_1_out), .Q(test[7]), .reset(not_3_out), .en(1'b1));  // open: Qn, preset
  buf buffer_5 (buffer_5_out, D1);
  and and_4 (and_4_out, not_1_out, buffer_5_out);
  and and_5 (and_5_out, test[6], not_2_out);
  S_R_Flip_Flop #(.trigger("falling")) s_r_ff_2 (
    .S(not_5_out), .clk(nor_2_out), .R(nor_3_out), .Q(test[6]), .reset(not_3_out), .en(1'b1));  // open: Qn, preset
  buf buffer_6 (buffer_6_out, D2);
  and and_6 (and_6_out, not_1_out, buffer_6_out);
  nor nor_4 (nor_4_out, and_5_out, and_6_out);
  not not_6 (not_6_out, nor_4_out);
  S_R_Flip_Flop #(.trigger("falling")) s_r_ff_3 (
    .S(not_6_out), .clk(nor_2_out), .R(nor_4_out), .Q(test[5]), .reset(not_3_out), .en(1'b1));  // open: Qn, preset
  buf buffer_7 (buffer_7_out, D3);
  and and_7 (and_7_out, not_1_out, buffer_7_out);
  and and_8 (and_8_out, test[5], not_2_out);
  nor nor_5 (nor_5_out, and_8_out, and_7_out);
  not not_7 (not_7_out, nor_5_out);
  and and_9 (and_9_out, test[4], not_2_out);
  nor nor_6 (nor_6_out, and_9_out, and_10_out);
  not not_8 (not_8_out, nor_6_out);
  S_R_Flip_Flop #(.trigger("falling")) s_r_ff_4 (
    .S(not_7_out), .clk(nor_2_out), .R(nor_5_out), .Q(test[4]), .reset(not_3_out), .en(1'b1));  // open: Qn, preset
  buf buffer_8 (buffer_8_out, D4);
  and and_10 (and_10_out, not_1_out, buffer_8_out);
  S_R_Flip_Flop #(.trigger("falling")) s_r_ff_5 (
    .S(not_8_out), .clk(nor_2_out), .R(nor_6_out), .Q(test[3]), .reset(not_3_out), .en(1'b1));  // open: Qn, preset
  buf buffer_9 (buffer_9_out, D5);
  and and_11 (and_11_out, not_1_out, buffer_9_out);
  and and_12 (and_12_out, test[3], not_2_out);
  nor nor_7 (nor_7_out, and_12_out, and_11_out);
  not not_9 (not_9_out, nor_7_out);
  S_R_Flip_Flop #(.trigger("falling")) s_r_ff_6 (
    .S(not_9_out), .clk(nor_2_out), .R(nor_7_out), .Q(test[2]), .reset(not_3_out), .en(1'b1));  // open: Qn, preset
  and and_13 (and_13_out, not_1_out, buffer_10_out);
  and and_14 (and_14_out, test[2], not_2_out);
  nor nor_8 (nor_8_out, and_14_out, and_13_out);
  not not_10 (not_10_out, nor_8_out);
  buf buffer_10 (buffer_10_out, D6);
  and and_15 (and_15_out, test[1], not_2_out);
  S_R_Flip_Flop #(.trigger("falling")) s_r_ff_7 (
    .S(not_10_out), .clk(nor_2_out), .R(nor_8_out), .Q(test[1]), .reset(not_3_out), .en(1'b1));  // open: Qn, preset
  buf buffer_11 (buffer_11_out, D7);
  and and_16 (and_16_out, not_1_out, buffer_11_out);
  nor nor_9 (nor_9_out, and_15_out, and_16_out);
  not not_11 (not_11_out, nor_9_out);
  S_R_Flip_Flop #(.trigger("falling")) s_r_ff_8 (
    .S(not_11_out), .clk(nor_2_out), .R(nor_9_out), .Q(s_r_ff_8_q), .reset(not_3_out), .en(1'b1));  // open: Qn, preset
  buf buffer_12 (Q7, s_r_ff_8_q);

  assign test[0] = Q7;
endmodule

module _74299 (
  input  DSR,
  input  S0,
  input  S1,
  input  CP,
  input  OE1,
  input  OE2,
  input  [7:0] in,
  input  DSL,
  input  MR,
  output [7:0] test,
  output Q0,
  output [7:0] out,
  output Q7
);

  wire and_1_out, and_2_out, and_3_out, and_4_out, and_5_out, and_6_out, and_7_out, and_8_out, and_9_out,
       and_10_out, and_11_out, and_12_out, and_13_out, and_14_out, and_15_out, and_16_out, and_17_out,
       and_18_out, and_19_out, and_20_out, and_21_out, and_22_out, and_23_out, and_24_out, and_25_out,
       and_26_out, and_27_out, and_28_out, and_29_out, and_30_out, and_31_out, and_32_out, buffer_1_out,
       buffer_2_out, buffer_3_out, buffer_6_out, buffer_7_out, buffer_8_out, buffer_9_out, buffer_10_out,
       buffer_11_out, buffer_12_out, buffer_13_out, nand_1_out, nand_2_out, not_1_out, not_2_out, not_3_out,
       not_4_out, not_5_out, not_6_out, not_7_out, or_1_out, or_2_out, or_3_out, or_4_out, or_5_out,
       or_6_out, or_7_out, or_8_out;

  nand nand_1 (nand_1_out, S0, S1);
  buf buffer_1 (buffer_1_out, DSR);
  not not_1 (not_1_out, buffer_2_out);
  buf buffer_2 (buffer_2_out, S0);
  buf buffer_3 (buffer_3_out, S1);
  not not_2 (not_2_out, buffer_3_out);
  not not_3 (not_3_out, CP);
  buf buffer_4 (Q0, test[0]);
  nand nand_2 (nand_2_out, nand_1_out, ~OE1, ~OE2);  // NAND_Gate
  not not_4 (not_4_out, not_1_out);
  not not_5 (not_5_out, not_2_out);
  buf buffer_5 (Q7, test[7]);
  not not_6 (not_6_out, MR);
  and and_1 (and_1_out, buffer_1_out, not_4_out, not_2_out);
  and and_2 (and_2_out, not_5_out, not_1_out, test[1]);
  and and_3 (and_3_out, not_5_out, not_4_out, buffer_6_out);
  and and_4 (and_4_out, not_2_out, not_1_out, test[0]);
  and and_5 (and_5_out, test[0], not_4_out, not_2_out);
  and and_6 (and_6_out, not_5_out, not_1_out, test[2]);
  and and_7 (and_7_out, not_5_out, not_4_out, buffer_7_out);
  and and_8 (and_8_out, not_2_out, not_1_out, test[1]);
  and and_9 (and_9_out, test[1], not_4_out, not_2_out);
  and and_10 (and_10_out, not_5_out, not_1_out, test[3]);
  and and_11 (and_11_out, not_5_out, not_4_out, buffer_8_out);
  and and_12 (and_12_out, not_2_out, not_1_out, test[2]);
  and and_13 (and_13_out, test[2], not_4_out, not_2_out);
  and and_14 (and_14_out, not_5_out, not_1_out, test[4]);
  and and_15 (and_15_out, not_5_out, not_4_out, buffer_9_out);
  and and_16 (and_16_out, not_2_out, not_1_out, test[3]);
  and and_17 (and_17_out, test[3], not_4_out, not_2_out);
  and and_18 (and_18_out, not_5_out, not_1_out, test[5]);
  and and_19 (and_19_out, not_5_out, not_4_out, buffer_10_out);
  and and_20 (and_20_out, not_2_out, not_1_out, test[4]);
  and and_21 (and_21_out, test[4], not_4_out, not_2_out);
  and and_22 (and_22_out, not_5_out, not_1_out, test[6]);
  and and_23 (and_23_out, not_5_out, not_4_out, buffer_11_out);
  and and_24 (and_24_out, not_2_out, not_1_out, test[5]);
  and and_25 (and_25_out, test[5], not_4_out, not_2_out);
  and and_26 (and_26_out, not_5_out, not_1_out, test[7]);
  and and_27 (and_27_out, not_5_out, not_4_out, buffer_12_out);
  and and_28 (and_28_out, not_2_out, not_1_out, test[6]);
  and and_29 (and_29_out, test[6], not_4_out, not_2_out);
  and and_30 (and_30_out, not_5_out, not_1_out, DSL);
  and and_31 (and_31_out, not_5_out, not_4_out, buffer_13_out);
  and and_32 (and_32_out, not_2_out, not_1_out, test[7]);
  or or_1 (or_1_out, and_1_out, and_2_out, and_3_out, and_4_out);
  or or_2 (or_2_out, and_5_out, and_6_out, and_7_out, and_8_out);
  or or_3 (or_3_out, and_9_out, and_10_out, and_11_out, and_12_out);
  or or_4 (or_4_out, and_13_out, and_14_out, and_15_out, and_16_out);
  or or_5 (or_5_out, and_17_out, and_18_out, and_19_out, and_20_out);
  or or_6 (or_6_out, and_21_out, and_22_out, and_23_out, and_24_out);
  or or_7 (or_7_out, and_25_out, and_26_out, and_27_out, and_28_out);
  or or_8 (or_8_out, and_29_out, and_30_out, and_31_out, and_32_out);
  buf buffer_6 (buffer_6_out, in[0]);
  assign out[0] = not_7_out ? test[0] : 1'bz;  // Controlled_Buffer controlled_buffer_1
  D_Flip_Flop #(.trigger("falling")) d_ff_1 (
    .clk(not_3_out), .D(or_1_out), .Q(test[0]), .reset(not_6_out));  // open: Qn, preset, en
  not not_7 (not_7_out, nand_2_out);
  buf buffer_7 (buffer_7_out, in[1]);
  D_Flip_Flop #(.trigger("falling")) d_ff_2 (
    .clk(not_3_out), .D(or_2_out), .Q(test[1]), .reset(not_6_out));  // open: Qn, preset, en
  assign out[1] = not_7_out ? test[1] : 1'bz;  // Controlled_Buffer controlled_buffer_2
  buf buffer_8 (buffer_8_out, in[2]);
  assign out[2] = not_7_out ? test[2] : 1'bz;  // Controlled_Buffer controlled_buffer_3
  D_Flip_Flop #(.trigger("falling")) d_ff_3 (
    .clk(not_3_out), .D(or_3_out), .Q(test[2]), .reset(not_6_out));  // open: Qn, preset, en
  buf buffer_9 (buffer_9_out, in[3]);
  D_Flip_Flop #(.trigger("falling")) d_ff_4 (
    .clk(not_3_out), .D(or_4_out), .Q(test[3]), .reset(not_6_out));  // open: Qn, preset, en
  assign out[3] = not_7_out ? test[3] : 1'bz;  // Controlled_Buffer controlled_buffer_4
  buf buffer_10 (buffer_10_out, in[4]);
  D_Flip_Flop #(.trigger("falling")) d_ff_5 (
    .clk(not_3_out), .D(or_5_out), .Q(test[4]), .reset(not_6_out));  // open: Qn, preset, en
  assign out[4] = not_7_out ? test[4] : 1'bz;  // Controlled_Buffer controlled_buffer_5
  buf buffer_11 (buffer_11_out, in[5]);
  D_Flip_Flop #(.trigger("falling")) d_ff_6 (
    .clk(not_3_out), .D(or_6_out), .Q(test[5]), .reset(not_6_out));  // open: Qn, preset, en
  assign out[5] = not_7_out ? test[5] : 1'bz;  // Controlled_Buffer controlled_buffer_6
  buf buffer_12 (buffer_12_out, in[6]);
  D_Flip_Flop #(.trigger("falling")) d_ff_7 (
    .clk(not_3_out), .D(or_7_out), .Q(test[6]), .reset(not_6_out));  // open: Qn, preset, en
  assign out[6] = not_7_out ? test[6] : 1'bz;  // Controlled_Buffer controlled_buffer_7
  buf buffer_13 (buffer_13_out, in[7]);
  D_Flip_Flop #(.trigger("falling")) d_ff_8 (
    .clk(not_3_out), .D(or_8_out), .Q(test[7]), .reset(not_6_out));  // open: Qn, preset, en
  assign out[7] = not_7_out ? test[7] : 1'bz;  // Controlled_Buffer controlled_buffer_8
endmodule

module _74181 (
  input  S3,
  input  S2,
  input  S1,
  input  S0,
  input  B3,
  input  A3,
  input  B2,
  input  A2,
  input  B1,
  input  A1,
  input  B0,
  input  A0,
  input  M,
  input  Cn,
  output G,
  output Cn_4,
  output P,
  output F3,
  output F2,
  output A_B,
  output F1,
  output F0
);

  wire and_1_out, and_2_out, and_3_out, and_4_out, and_5_out, and_6_out, and_7_out, and_8_out, and_9_out,
       and_10_out, and_11_out, and_12_out, and_13_out, and_14_out, and_15_out, and_16_out, and_17_out,
       and_18_out, and_19_out, and_20_out, and_21_out, and_22_out, and_23_out, and_24_out, and_25_out,
       and_26_out, and_28_out, and_29_out, and_30_out, and_31_out, and_32_out, and_33_out, and_34_out,
       and_35_out, and_36_out, and_37_out, and_38_out, nand_3_out, nand_4_out, nor_2_out, nor_3_out,
       nor_4_out, nor_5_out, nor_6_out, nor_7_out, nor_8_out, nor_9_out, nor_10_out, nor_11_out, nor_12_out,
       not_1_out, not_2_out, not_3_out, not_4_out, not_5_out, not_6_out, not_7_out, not_8_out, not_9_out;

  and and_1 (and_1_out, nor_3_out, nor_3_out);
  nor nor_1 (G, and_1_out, and_3_out, and_2_out, and_5_out, and_5_out);
  and and_2 (and_2_out, nor_2_out, nor_4_out, nor_9_out);
  and and_3 (and_3_out, nor_2_out, nor_6_out);
  and and_4 (and_4_out, B3, S3, A3);
  nand nand_1 (Cn_4, G, nand_3_out);
  and and_5 (and_5_out, nor_2_out, nor_4_out, nor_7_out, nor_12_out, nor_12_out);
  nor nor_2 (nor_2_out, and_4_out, and_6_out);
  and and_6 (and_6_out, A3, S2, not_1_out);
  not not_1 (not_1_out, B3);
  nand nand_2 (P, nor_2_out, nor_4_out, nor_7_out, nor_11_out, nor_11_out);
  nand nand_3 (nand_3_out, nor_2_out, nor_4_out, nor_7_out, nor_11_out, Cn);
  nor nor_3 (nor_3_out, and_7_out, and_8_out, and_10_out);
  and and_7 (and_7_out, not_1_out, S1);
  and and_8 (and_8_out, S0, B3);
  and and_9 (and_9_out, nor_2_out, not_2_out);
  not not_2 (not_2_out, nor_3_out);
  and and_10 (and_10_out, A3, A3);
  and and_11 (and_11_out, nor_4_out, nor_7_out, nor_11_out, Cn, not_9_out);
  nor nor_4 (nor_4_out, and_12_out, and_13_out);
  and and_12 (and_12_out, B2, S3, A2);
  and and_13 (and_13_out, A2, S2, not_3_out);
  xor xor_1 (F3, and_9_out, nor_5_out);
  nor nor_5 (nor_5_out, and_11_out, and_15_out, and_14_out, and_18_out, and_18_out);
  and and_14 (and_14_out, nor_4_out, nor_9_out, not_9_out);
  and and_15 (and_15_out, nor_4_out, nor_7_out, nor_12_out, not_9_out, not_9_out);
  nor nor_6 (nor_6_out, and_16_out, and_17_out, and_19_out);
  and and_16 (and_16_out, not_3_out, S1);
  and and_17 (and_17_out, S0, B2);
  not not_3 (not_3_out, B2);
  and and_18 (and_18_out, nor_6_out, not_9_out);
  and and_19 (and_19_out, A2, A2);
  and and_20 (and_20_out, nor_4_out, not_4_out);
  and and_21 (and_21_out, nor_7_out, nor_7_out, nor_11_out, Cn, not_9_out);
  not not_4 (not_4_out, nor_6_out);
  nor nor_7 (nor_7_out, and_22_out, and_25_out);
  and and_22 (and_22_out, B1, S3, A1);
  xor xor_2 (F2, and_20_out, nor_8_out);
  nor nor_8 (nor_8_out, and_21_out, and_23_out, and_24_out);
  and and_23 (and_23_out, nor_7_out, nor_12_out, not_9_out);
  and and_24 (and_24_out, nor_9_out, not_9_out);
  and and_25 (and_25_out, A1, S2, not_5_out);
  and and_26 (and_26_out, not_5_out, S1);
  not not_5 (not_5_out, B1);
  and and_27 (A_B, F3, F3, F2, F1, F0);
  and and_28 (and_28_out, nor_7_out, not_6_out);
  not not_6 (not_6_out, nor_9_out);
  nor nor_9 (nor_9_out, and_26_out, and_29_out, and_30_out);
  and and_29 (and_29_out, S0, B1);
  and and_30 (and_30_out, A1, A1);
  xor xor_3 (F1, and_28_out, nor_10_out);
  and and_31 (and_31_out, Cn, nor_11_out, not_9_out);
  and and_32 (and_32_out, B0, S3, A0);
  nor nor_10 (nor_10_out, and_31_out, and_33_out);
  and and_33 (and_33_out, nor_12_out, not_9_out);
  nor nor_11 (nor_11_out, and_32_out, and_34_out);
  and and_34 (and_34_out, A0, S2, not_7_out);
  not not_7 (not_7_out, B0);
  and and_35 (and_35_out, nor_11_out, not_8_out);
  not not_8 (not_8_out, nor_12_out);
  nor nor_12 (nor_12_out, and_37_out, and_36_out, and_38_out);
  and and_36 (and_36_out, S0, B0);
  and and_37 (and_37_out, not_7_out, S1);
  xor xor_4 (F0, and_35_out, nand_4_out);
  nand nand_4 (nand_4_out, not_9_out, Cn);
  and and_38 (and_38_out, A0, A0);
  not not_9 (not_9_out, M);
endmodule

module _74381 (
  input  Cn,
  input  B0,
  input  A0,
  input  B1,
  input  A1,
  input  B2,
  input  A2,
  input  B3,
  input  A3,
  input  S0,
  input  S1,
  input  S2,
  output F0,
  output F1,
  output F2,
  output F3,
  output P,
  output G
);

  wire and_1_out, and_2_out, and_3_out, and_4_out, and_5_out, and_6_out, and_7_out, and_8_out, and_9_out,
       and_10_out, and_11_out, and_12_out, and_13_out, and_14_out, and_15_out, and_16_out, and_17_out,
       and_18_out, and_19_out, and_20_out, and_21_out, and_22_out, and_23_out, and_24_out, and_25_out,
       and_26_out, and_27_out, and_28_out, and_29_out, and_30_out, and_31_out, and_32_out, and_33_out,
       and_34_out, and_35_out, and_36_out, and_37_out, and_38_out, and_39_out, and_40_out, and_41_out,
       and_42_out, and_43_out, and_44_out, nand_1_out, nand_3_out, nand_4_out, nand_5_out, nand_6_out,
       nor_1_out, nor_2_out, nor_3_out, nor_4_out, nor_5_out, nor_6_out, nor_7_out, nor_8_out, nor_9_out,
       nor_10_out, nor_11_out, nor_12_out, nor_14_out, not_1_out, not_2_out, not_3_out, not_4_out, not_5_out,
       not_6_out, not_7_out, not_8_out, not_9_out, not_10_out, not_11_out, not_12_out, not_13_out, not_14_out;

  and and_1 (and_1_out, not_2_out, not_2_out, not_1_out, nand_3_out, nand_6_out);
  nor nor_1 (nor_1_out, and_1_out, and_2_out, and_3_out);
  and and_2 (and_2_out, nand_4_out, nand_3_out, nand_5_out, not_1_out, A0);
  not not_1 (not_1_out, B0);
  and and_3 (and_3_out, nand_6_out, nand_6_out, nand_5_out, B0, not_2_out);
  nand nand_1 (nand_1_out, Cn, nor_12_out);
  and and_4 (and_4_out, not_2_out, not_1_out, nand_4_out, nand_5_out, nor_14_out);
  and and_5 (and_5_out, nand_6_out, nand_6_out, nand_3_out, not_1_out, A0);
  not not_2 (not_2_out, A0);
  xor xor_1 (F0, nand_1_out, nor_2_out);
  nor nor_2 (nor_2_out, and_4_out, and_4_out, and_5_out, and_6_out, and_7_out);
  and and_6 (and_6_out, nand_6_out, nand_6_out, nand_3_out, B0, not_2_out);
  and and_7 (and_7_out, nand_4_out, nand_4_out, nand_5_out, B0, A0);
  and and_8 (and_8_out, not_4_out, not_4_out, not_3_out, nand_3_out, nand_6_out);
  nor nor_3 (nor_3_out, and_8_out, and_9_out, and_11_out);
  and and_9 (and_9_out, nand_4_out, nand_3_out, nand_5_out, not_3_out, A1);
  not not_3 (not_3_out, B1);
  and and_10 (and_10_out, not_4_out, not_3_out, nand_4_out, nand_5_out, nor_14_out);
  and and_11 (and_11_out, nand_6_out, nand_6_out, nand_5_out, B1, not_4_out);
  xor xor_2 (F1, nor_4_out, nor_5_out);
  nor nor_4 (nor_4_out, and_12_out, and_13_out);
  and and_12 (and_12_out, Cn, nor_1_out, nor_12_out);
  and and_13 (and_13_out, nor_1_out, nor_2_out, nor_12_out);
  nor nor_5 (nor_5_out, and_10_out, and_10_out, and_14_out, and_15_out, and_16_out);
  and and_14 (and_14_out, nand_6_out, nand_6_out, nand_3_out, not_3_out, A1);
  not not_4 (not_4_out, A1);
  and and_15 (and_15_out, nand_6_out, nand_6_out, nand_3_out, B1, not_4_out);
  and and_16 (and_16_out, nand_4_out, nand_4_out, nand_5_out, B1, A1);
  and and_17 (and_17_out, not_6_out, not_6_out, not_5_out, nand_3_out, nand_6_out);
  not not_5 (not_5_out, B2);
  and and_18 (and_18_out, Cn, Cn, nor_1_out, nor_3_out, nor_12_out);
  nor nor_6 (nor_6_out, and_17_out, and_19_out, and_20_out);
  and and_19 (and_19_out, nand_4_out, nand_3_out, nand_5_out, not_5_out, A2);
  and and_20 (and_20_out, nand_6_out, nand_6_out, nand_5_out, B2, not_6_out);
  nor nor_7 (nor_7_out, and_18_out, and_21_out, and_23_out);
  and and_21 (and_21_out, nor_1_out, nor_1_out, nor_3_out, nor_2_out, nor_12_out);
  and and_22 (and_22_out, not_6_out, not_5_out, nand_4_out, nand_5_out, nor_14_out);
  xor xor_3 (F2, nor_7_out, nor_8_out);
  and and_23 (and_23_out, nor_3_out, nor_5_out, nor_12_out);
  nor nor_8 (nor_8_out, and_22_out, and_22_out, and_24_out, and_26_out, and_25_out);
  and and_24 (and_24_out, nand_6_out, nand_6_out, nand_3_out, not_5_out, A2);
  not not_6 (not_6_out, A2);
  and and_25 (and_25_out, nand_4_out, nand_4_out, nand_5_out, B2, A2);
  and and_26 (and_26_out, nand_6_out, nand_6_out, nand_3_out, B2, not_6_out);
  and and_27 (and_27_out, Cn, nor_1_out, nor_3_out, nor_6_out, nor_12_out);
  nor nor_9 (nor_9_out, and_28_out, and_29_out, and_32_out);
  and and_28 (and_28_out, not_8_out, not_8_out, not_7_out, nand_3_out, nand_6_out);
  and and_29 (and_29_out, nand_4_out, nand_3_out, nand_5_out, not_7_out, A3);
  not not_7 (not_7_out, B3);
  nor nor_10 (nor_10_out, and_27_out, and_27_out, and_30_out, and_31_out, and_33_out);
  and and_30 (and_30_out, nor_1_out, nor_3_out, nor_6_out, nor_2_out, nor_12_out);
  and and_31 (and_31_out, nor_3_out, nor_3_out, nor_6_out, nor_5_out, nor_12_out);
  and and_32 (and_32_out, nand_6_out, nand_6_out, nand_5_out, B3, not_8_out);
  and and_33 (and_33_out, nor_6_out, nor_8_out, nor_12_out);
  and and_34 (and_34_out, not_8_out, not_7_out, nand_4_out, nand_5_out, nor_14_out);
  not not_8 (not_8_out, A3);
  xor xor_4 (F3, nor_10_out, nor_11_out);
  nor nor_11 (nor_11_out, and_34_out, and_34_out, and_36_out, and_35_out, and_37_out);
  and and_35 (and_35_out, nand_6_out, nand_6_out, nand_3_out, B3, not_8_out);
  and and_36 (and_36_out, nand_6_out, nand_6_out, nand_3_out, not_7_out, A3);
  nand nand_2 (P, nor_1_out, nor_1_out, nor_3_out, nor_6_out, nor_9_out);
  nor nor_12 (nor_12_out, not_14_out, and_40_out);
  and and_37 (and_37_out, nand_4_out, nand_4_out, nand_5_out, B3, A3);
  and and_38 (and_38_out, nor_3_out, nor_3_out, nor_6_out, nor_9_out, nor_5_out);
  and and_39 (and_39_out, nor_1_out, nor_3_out, nor_6_out, nor_9_out, nor_2_out);
  and and_40 (and_40_out, not_9_out, not_11_out);
  nor nor_13 (G, and_39_out, and_39_out, and_38_out, and_41_out, and_43_out);
  and and_41 (and_41_out, nor_6_out, nor_9_out, nor_8_out);
  and and_42 (and_42_out, not_9_out, not_14_out);
  nand nand_3 (nand_3_out, not_9_out, not_12_out);
  nand nand_4 (nand_4_out, not_9_out, not_11_out);
  not not_9 (not_9_out, S0);
  and and_43 (and_43_out, nor_9_out, nor_11_out);
  nor nor_14 (nor_14_out, and_42_out, and_44_out);
  and and_44 (and_44_out, not_11_out, not_14_out);
  nand nand_5 (nand_5_out, not_10_out, not_12_out, not_13_out);
  nand nand_6 (nand_6_out, not_11_out, not_13_out);
  not not_10 (not_10_out, not_9_out);
  not not_11 (not_11_out, S1);
  not not_12 (not_12_out, not_11_out);
  not not_13 (not_13_out, S2);
  not not_14 (not_14_out, not_13_out);
endmodule

module _74382 (
  input  Cn,
  input  B0,
  input  A0,
  input  B1,
  input  A1,
  input  B2,
  input  A2,
  input  B3,
  input  A3,
  input  S0,
  input  S1,
  input  S2,
  output F0,
  output F1,
  output F2,
  output F3,
  output OVR,
  output Cn_4
);

  wire and_1_out, and_2_out, and_3_out, and_4_out, and_5_out, and_6_out, and_7_out, and_8_out, and_9_out,
       and_10_out, and_11_out, and_12_out, and_13_out, and_14_out, and_15_out, and_16_out, and_17_out,
       and_18_out, and_19_out, and_20_out, and_21_out, and_22_out, and_23_out, and_24_out, and_25_out,
       and_26_out, and_27_out, and_28_out, and_29_out, and_30_out, and_31_out, and_32_out, and_33_out,
       and_34_out, and_35_out, and_36_out, and_37_out, and_38_out, and_39_out, and_40_out, and_41_out,
       and_42_out, and_43_out, and_44_out, and_45_out, nand_1_out, nand_2_out, nand_3_out, nand_4_out,
       nand_6_out, nand_7_out, nor_1_out, nor_2_out, nor_3_out, nor_4_out, nor_5_out, nor_6_out, nor_7_out,
       nor_8_out, nor_9_out, nor_10_out, nor_11_out, nor_12_out, nor_13_out, nor_14_out, not_1_out,
       not_2_out, not_3_out, not_4_out, not_5_out, not_6_out, not_7_out, not_8_out, not_9_out, not_10_out,
       not_11_out, not_12_out, not_13_out, not_14_out;

  and and_1 (and_1_out, not_2_out, not_2_out, not_1_out, nand_3_out, nand_7_out);
  nor nor_1 (nor_1_out, and_1_out, and_2_out, and_4_out);
  and and_2 (and_2_out, nand_4_out, nand_3_out, nand_2_out, not_1_out, A0);
  not not_1 (not_1_out, B0);
  and and_3 (and_3_out, not_2_out, not_1_out, nand_4_out, nand_2_out, nor_14_out);
  and and_4 (and_4_out, nand_7_out, nand_7_out, nand_2_out, B0, not_2_out);
  xor xor_1 (F0, nand_1_out, nor_2_out);
  nand nand_1 (nand_1_out, Cn, nor_12_out);
  nor nor_2 (nor_2_out, and_3_out, and_3_out, and_5_out, and_6_out, and_7_out);
  and and_5 (and_5_out, nand_7_out, nand_7_out, nand_3_out, not_1_out, A0);
  not not_2 (not_2_out, A0);
  and and_6 (and_6_out, nand_7_out, nand_7_out, nand_3_out, B0, not_2_out);
  and and_7 (and_7_out, nand_4_out, nand_4_out, nand_2_out, B0, A0);
  and and_8 (and_8_out, not_4_out, not_4_out, not_3_out, nand_3_out, nand_7_out);
  not not_3 (not_3_out, B1);
  nor nor_3 (nor_3_out, and_8_out, and_10_out, and_9_out);
  and and_9 (and_9_out, nand_7_out, nand_7_out, nand_2_out, B1, not_4_out);
  and and_10 (and_10_out, nand_4_out, nand_3_out, nand_2_out, not_3_out, A1);
  and and_11 (and_11_out, Cn, nor_1_out, nor_12_out);
  and and_12 (and_12_out, not_4_out, not_3_out, nand_4_out, nand_2_out, nor_14_out);
  xor xor_2 (F1, nor_4_out, nor_5_out);
  nor nor_4 (nor_4_out, and_11_out, and_13_out);
  and and_13 (and_13_out, nor_1_out, nor_2_out, nor_12_out);
  nor nor_5 (nor_5_out, and_12_out, and_12_out, and_14_out, and_15_out, and_16_out);
  and and_14 (and_14_out, nand_7_out, nand_7_out, nand_3_out, not_3_out, A1);
  not not_4 (not_4_out, A1);
  and and_15 (and_15_out, nand_7_out, nand_7_out, nand_3_out, B1, not_4_out);
  and and_16 (and_16_out, nand_4_out, nand_4_out, nand_2_out, B1, A1);
  nor nor_6 (nor_6_out, and_18_out, and_17_out, and_20_out);
  and and_17 (and_17_out, nand_4_out, nand_3_out, nand_2_out, not_5_out, A2);
  and and_18 (and_18_out, not_6_out, not_6_out, not_5_out, nand_3_out, nand_7_out);
  not not_5 (not_5_out, B2);
  and and_19 (and_19_out, Cn, Cn, nor_1_out, nor_3_out, nor_12_out);
  and and_20 (and_20_out, nand_7_out, nand_7_out, nand_2_out, B2, not_6_out);
  nor nor_7 (nor_7_out, and_19_out, and_21_out, and_23_out);
  and and_21 (and_21_out, nor_1_out, nor_1_out, nor_3_out, nor_2_out, nor_12_out);
  and and_22 (and_22_out, not_6_out, not_5_out, nand_4_out, nand_2_out, nor_14_out);
  not not_6 (not_6_out, A2);
  xor xor_3 (F2, nor_7_out, nor_8_out);
  and and_23 (and_23_out, nor_3_out, nor_5_out, nor_12_out);
  nor nor_8 (nor_8_out, and_22_out, and_22_out, and_24_out, and_25_out, and_26_out);
  and and_24 (and_24_out, nand_7_out, nand_7_out, nand_3_out, not_5_out, A2);
  and and_25 (and_25_out, nand_7_out, nand_7_out, nand_3_out, B2, not_6_out);
  and and_26 (and_26_out, nand_4_out, nand_4_out, nand_2_out, B2, A2);
  and and_27 (and_27_out, not_8_out, not_8_out, not_7_out, nand_3_out, nand_7_out);
  and and_28 (and_28_out, Cn, nor_1_out, nor_3_out, nor_6_out, nor_12_out);
  and and_29 (and_29_out, nor_1_out, nor_3_out, nor_6_out, nor_2_out, nor_12_out);
  nor nor_9 (nor_9_out, and_27_out, and_30_out, and_32_out);
  and and_30 (and_30_out, nand_4_out, nand_3_out, nand_2_out, not_7_out, A3);
  not not_7 (not_7_out, B3);
  nor nor_10 (nor_10_out, and_28_out, and_28_out, and_29_out, and_31_out, and_33_out);
  and and_31 (and_31_out, nor_3_out, nor_3_out, nor_6_out, nor_5_out, nor_12_out);
  and and_32 (and_32_out, nand_7_out, nand_7_out, nand_2_out, B3, not_8_out);
  and and_33 (and_33_out, nor_6_out, nor_8_out, nor_12_out);
  and and_34 (and_34_out, not_8_out, not_7_out, nand_4_out, nand_2_out, nor_14_out);
  and and_35 (and_35_out, nand_7_out, nand_7_out, nand_3_out, not_7_out, A3);
  not not_8 (not_8_out, A3);
  xor xor_4 (F3, nor_10_out, nor_11_out);
  nor nor_11 (nor_11_out, and_34_out, and_34_out, and_35_out, and_36_out, and_38_out);
  and and_36 (and_36_out, nand_7_out, nand_7_out, nand_3_out, B3, not_8_out);
  and and_37 (and_37_out, nor_1_out, nor_3_out, nor_6_out, nor_9_out, nor_2_out);
  nor nor_12 (nor_12_out, not_13_out, and_40_out);
  and and_38 (and_38_out, nand_4_out, nand_4_out, nand_2_out, B3, A3);
  nor nor_13 (nor_13_out, and_37_out, and_37_out, and_39_out, and_43_out, and_42_out);
  and and_39 (and_39_out, nor_3_out, nor_3_out, nor_6_out, nor_9_out, nor_5_out);
  and and_40 (and_40_out, not_10_out, not_11_out);
  xor xor_5 (OVR, nor_10_out, and_41_out);
  and and_41 (and_41_out, nor_13_out, nand_6_out);
  and and_42 (and_42_out, nor_9_out, nor_11_out);
  and and_43 (and_43_out, nor_6_out, nor_9_out, nor_8_out);
  and and_44 (and_44_out, not_10_out, not_13_out);
  nand nand_2 (nand_2_out, not_9_out, not_12_out, not_14_out);
  nand nand_3 (nand_3_out, not_10_out, not_12_out);
  nand nand_4 (nand_4_out, not_10_out, not_11_out);
  not not_9 (not_9_out, not_10_out);
  not not_10 (not_10_out, S0);
  nand nand_5 (Cn_4, nor_13_out, nand_6_out);
  nand nand_6 (nand_6_out, Cn, nor_1_out, nor_3_out, nor_6_out, nor_9_out);
  nor nor_14 (nor_14_out, and_44_out, and_45_out);
  and and_45 (and_45_out, not_11_out, not_13_out);
  nand nand_7 (nand_7_out, not_11_out, not_14_out);
  not not_11 (not_11_out, S1);
  not not_12 (not_12_out, not_11_out);
  not not_13 (not_13_out, not_14_out);
  not not_14 (not_14_out, S2);
endmodule

module _74182 (
  input  G0,
  input  P0,
  input  Cn,
  input  G1,
  input  P1,
  input  G2,
  input  P2,
  input  G3,
  input  P3,
  output Cn_x,
  output Cn_y,
  output Cn_z,
  output G,
  output P
);

  wire and_1_out, and_2_out, and_3_out, and_4_out, and_5_out, and_6_out, and_7_out, and_8_out, and_9_out,
       and_10_out, and_11_out, and_12_out, and_13_out, not_1_out;

  nor nor_1 (Cn_x, and_1_out, and_2_out);
  and and_1 (and_1_out, G0, P0);
  and and_2 (and_2_out, G0, not_1_out);
  not not_1 (not_1_out, Cn);
  and and_3 (and_3_out, G1, P1);
  nor nor_2 (Cn_y, and_3_out, and_5_out, and_4_out);
  and and_4 (and_4_out, not_1_out, G0, G1);
  and and_5 (and_5_out, G0, P0, G1);
  and and_6 (and_6_out, G2, P2);
  nor nor_3 (Cn_z, and_6_out, and_7_out, and_8_out, and_9_out);
  and and_7 (and_7_out, G1, P1, G2);
  and and_8 (and_8_out, G0, G0, P0, G1, G2);
  and and_9 (and_9_out, not_1_out, not_1_out, G0, G1, G2);
  and and_10 (and_10_out, G3, P3);
  or or_1 (G, and_10_out, and_11_out, and_13_out, and_12_out);
  and and_11 (and_11_out, G2, P2, G3);
  and and_12 (and_12_out, G0, G0, G1, G2, G3);
  and and_13 (and_13_out, G1, G1, P1, G2, G3);
  or or_2 (P, P0, P1, P2, P3);
endmodule

module _74173 (
  input  D0,
  input  D1,
  input  D2,
  input  D3,
  input  nE1,
  input  nE2,
  input  CLK,
  input  MR,
  input  nOE1,
  input  nOE2,
  output Q0,
  output Q1,
  output Q2,
  output Q3
);

  wire and_1_out, and_2_out, and_3_out, and_4_out, and_5_out, and_6_out, and_7_out, and_8_out, and_9_out,
       and_10_out, buffer_1_out, buffer_2_out, buffer_3_out, buffer_4_out, buffer_5_out, buffer_6_out,
       buffer_7_out, buffer_8_out, buffer_9_out, buffer_10_out, buffer_11_out, d_ff_1_q, d_ff_1_qn, d_ff_2_q,
       d_ff_2_qn, d_ff_3_q, d_ff_3_qn, d_ff_4_q, d_ff_4_qn, not_1_out, not_2_out, or_1_out, or_2_out,
       or_3_out, or_4_out;

  buf buffer_1 (buffer_1_out, nE1);
  buf buffer_2 (buffer_2_out, nE2);
  buf buffer_3 (buffer_3_out, nOE1);
  buf buffer_4 (buffer_4_out, nOE2);
  and and_1 (and_1_out, ~buffer_1_out, ~buffer_2_out);  // AND_Gate
  buf buffer_5 (buffer_5_out, CLK);
  not not_1 (not_1_out, buffer_5_out);
  buf buffer_6 (buffer_6_out, buffer_7_out);
  buf buffer_7 (buffer_7_out, MR);
  and and_2 (and_2_out, ~buffer_3_out, ~buffer_4_out);  // AND_Gate
  buf buffer_8 (buffer_8_out, D0);
  not not_2 (not_2_out, and_1_out);
  and and_3 (and_3_out, and_1_out, buffer_8_out);
  or or_1 (or_1_out, and_3_out, and_4_out);
  and and_4 (and_4_out, not_2_out, d_ff_1_q);
  D_Flip_Flop #(.trigger("falling")) d_ff_1 (
    .clk(not_1_out), .D(or_1_out), .Q(d_ff_1_q), .Qn(d_ff_1_qn), .reset(buffer_6_out));  // open: preset, en
  assign Q0 = and_2_out ? ~d_ff_1_qn : 1'bz;  // Controlled_Inverter controlled_inverter_1
  buf buffer_9 (buffer_9_out, D1);
  and and_5 (and_5_out, and_1_out, buffer_9_out);
  and and_6 (and_6_out, not_2_out, d_ff_2_q);
  or or_2 (or_2_out, and_5_out, and_6_out);
  and and_7 (and_7_out, and_1_out, buffer_10_out);
  D_Flip_Flop #(.trigger("falling")) d_ff_2 (
    .clk(not_1_out), .D(or_2_out), .Q(d_ff_2_q), .Qn(d_ff_2_qn), .reset(buffer_6_out));  // open: preset, en
  assign Q1 = and_2_out ? ~d_ff_2_qn : 1'bz;  // Controlled_Inverter controlled_inverter_2
  buf buffer_10 (buffer_10_out, D2);
  and and_8 (and_8_out, not_2_out, d_ff_3_q);
  or or_3 (or_3_out, and_7_out, and_8_out);
  D_Flip_Flop #(.trigger("falling")) d_ff_3 (
    .clk(not_1_out), .D(or_3_out), .Q(d_ff_3_q), .Qn(d_ff_3_qn), .reset(buffer_6_out));  // open: preset, en
  assign Q2 = and_2_out ? ~d_ff_3_qn : 1'bz;  // Controlled_Inverter controlled_inverter_3
  buf buffer_11 (buffer_11_out, D3);
  and and_9 (and_9_out, and_1_out, buffer_11_out);
  or or_4 (or_4_out, and_9_out, and_10_out);
  and and_10 (and_10_out, not_2_out, d_ff_4_q);
  D_Flip_Flop #(.trigger("falling")) d_ff_4 (
    .clk(not_1_out), .D(or_4_out), .Q(d_ff_4_q), .Qn(d_ff_4_qn), .reset(buffer_6_out));  // open: preset, en
  assign Q3 = and_2_out ? ~d_ff_4_qn : 1'bz;  // Controlled_Inverter controlled_inverter_4
endmodule

module _74377 (
  input  D0,
  input  D1,
  input  D2,
  input  D3,
  input  D4,
  input  D5,
  input  D6,
  input  D7,
  input  EN,
  input  CLK,
  output Q0,
  output Q1,
  output Q2,
  output Q3,
  output Q4,
  output Q5,
  output Q6,
  output Q7
);

  wire and_1_out, and_2_out, and_3_out, and_4_out, and_5_out, and_6_out, and_7_out, and_8_out, and_9_out,
       and_10_out, and_11_out, and_12_out, and_13_out, and_14_out, and_15_out, and_16_out, buffer_1_out,
       buffer_2_out, buffer_3_out, buffer_4_out, buffer_5_out, buffer_6_out, buffer_7_out, buffer_8_out,
       buffer_9_out, d_ff_1_q, d_ff_2_q, d_ff_3_q, d_ff_4_q, d_ff_5_q, d_ff_6_q, d_ff_7_q, d_ff_8_q,
       not_1_out, not_2_out, or_1_out, or_2_out, or_3_out, or_4_out, or_5_out, or_6_out, or_7_out, or_8_out;

  buf buffer_1 (buffer_1_out, EN);
  not not_1 (not_1_out, buffer_1_out);
  not not_2 (not_2_out, CLK);
  buf buffer_2 (buffer_2_out, D0);
  and and_1 (and_1_out, not_1_out, d_ff_1_q);
  and and_2 (and_2_out, buffer_1_out, buffer_2_out);
  or or_1 (or_1_out, and_2_out, and_1_out);
  buf buffer_3 (buffer_3_out, D1);
  and and_3 (and_3_out, buffer_1_out, buffer_3_out);
  D_Flip_Flop #(.trigger("falling")) d_ff_1 (
    .clk(not_2_out), .D(or_1_out), .Q(d_ff_1_q), .Qn(Q0));  // open: preset, en, reset
  and and_4 (and_4_out, not_1_out, d_ff_2_q);
  or or_2 (or_2_out, and_3_out, and_4_out);
  D_Flip_Flop #(.trigger("falling")) d_ff_2 (
    .clk(not_2_out), .D(or_2_out), .Q(d_ff_2_q), .Qn(Q1));  // open: preset, en, reset
  buf buffer_4 (buffer_4_out, D2);
  and and_5 (and_5_out, not_1_out, d_ff_3_q);
  and and_6 (and_6_out, buffer_1_out, buffer_4_out);
  or or_3 (or_3_out, and_6_out, and_5_out);
  D_Flip_Flop #(.trigger("falling")) d_ff_3 (
    .clk(not_2_out), .D(or_3_out), .Q(d_ff_3_q), .Qn(Q2));  // open: preset, en, reset
  buf buffer_5 (buffer_5_out, D3);
  and and_7 (and_7_out, buffer_1_out, buffer_5_out);
  and and_8 (and_8_out, not_1_out, d_ff_4_q);
  or or_4 (or_4_out, and_7_out, and_8_out);
  D_Flip_Flop #(.trigger("falling")) d_ff_4 (
    .clk(not_2_out), .D(or_4_out), .Q(d_ff_4_q), .Qn(Q3));  // open: preset, en, reset
  buf buffer_6 (buffer_6_out, D4);
  and and_9 (and_9_out, buffer_1_out, buffer_6_out);
  or or_5 (or_5_out, and_9_out, and_10_out);
  and and_10 (and_10_out, not_1_out, d_ff_5_q);
  D_Flip_Flop #(.trigger("falling")) d_ff_5 (
    .clk(not_2_out), .D(or_5_out), .Q(d_ff_5_q), .Qn(Q4));  // open: preset, en, reset
  buf buffer_7 (buffer_7_out, D5);
  and and_11 (and_11_out, buffer_1_out, buffer_7_out);
  and and_12 (and_12_out, not_1_out, d_ff_6_q);
  or or_6 (or_6_out, and_11_out, and_12_out);
  and and_13 (and_13_out, buffer_1_out, buffer_8_out);
  D_Flip_Flop #(.trigger("falling")) d_ff_6 (
    .clk(not_2_out), .D(or_6_out), .Q(d_ff_6_q), .Qn(Q5));  // open: preset, en, reset
  buf buffer_8 (buffer_8_out, D6);
  and and_14 (and_14_out, not_1_out, d_ff_7_q);
  or or_7 (or_7_out, and_13_out, and_14_out);
  D_Flip_Flop #(.trigger("falling")) d_ff_7 (
    .clk(not_2_out), .D(or_7_out), .Q(d_ff_7_q), .Qn(Q6));  // open: preset, en, reset
  buf buffer_9 (buffer_9_out, D7);
  and and_15 (and_15_out, buffer_1_out, buffer_9_out);
  or or_8 (or_8_out, and_15_out, and_16_out);
  and and_16 (and_16_out, not_1_out, d_ff_8_q);
  D_Flip_Flop #(.trigger("falling")) d_ff_8 (
    .clk(not_2_out), .D(or_8_out), .Q(d_ff_8_q), .Qn(Q7));  // open: preset, en, reset
endmodule

module _7485 (
  input  A3,
  input  B3,
  input  A2,
  input  B2,
  input  A_B,
  input  A_B_2,
  input  A_B_3,
  input  A1,
  input  B1,
  input  A0,
  input  B0,
  output Qa_b,
  output Qa_b_2,
  output Qa_b_3
);

  wire and_1_out, and_2_out, and_3_out, and_4_out, and_5_out, and_6_out, and_7_out, and_8_out, and_9_out,
       and_10_out, and_11_out, and_12_out, and_13_out, and_14_out, and_15_out, and_16_out, and_17_out,
       and_18_out, and_19_out, and_20_out, buffer_1_out, buffer_2_out, buffer_3_out, buffer_4_out,
       buffer_5_out, buffer_6_out, buffer_7_out, buffer_8_out, buffer_9_out, buffer_10_out, buffer_11_out,
       nand_1_out, nand_2_out, nand_3_out, nand_4_out, nor_1_out, nor_2_out, nor_3_out, nor_4_out;

  buf buffer_1 (buffer_1_out, A3);
  buf buffer_2 (buffer_2_out, B3);
  buf buffer_3 (buffer_3_out, A2);
  buf buffer_4 (buffer_4_out, B2);
  buf buffer_5 (buffer_5_out, A_B);
  buf buffer_6 (buffer_6_out, A_B_2);
  buf buffer_7 (buffer_7_out, A_B_3);
  buf buffer_8 (buffer_8_out, A1);
  buf buffer_9 (buffer_9_out, B1);
  buf buffer_10 (buffer_10_out, A0);
  buf buffer_11 (buffer_11_out, B0);
  nand nand_1 (nand_1_out, buffer_1_out, buffer_2_out);
  nand nand_2 (nand_2_out, buffer_3_out, buffer_4_out);
  nand nand_3 (nand_3_out, buffer_8_out, buffer_9_out);
  nand nand_4 (nand_4_out, buffer_10_out, buffer_11_out);
  and and_1 (and_1_out, buffer_1_out, nand_1_out);
  and and_2 (and_2_out, nand_1_out, buffer_2_out);
  and and_3 (and_3_out, buffer_3_out, nand_2_out);
  and and_4 (and_4_out, nand_2_out, buffer_4_out);
  and and_5 (and_5_out, buffer_8_out, nand_3_out);
  and and_6 (and_6_out, nand_3_out, buffer_9_out);
  and and_7 (and_7_out, buffer_10_out, nand_4_out);
  and and_8 (and_8_out, nand_4_out, buffer_11_out);
  nor nor_1 (nor_1_out, and_1_out, and_2_out);
  nor nor_2 (nor_2_out, and_3_out, and_4_out);
  nor nor_3 (nor_3_out, and_5_out, and_6_out);
  nor nor_4 (nor_4_out, and_7_out, and_8_out);
  and and_9 (and_9_out, buffer_2_out, nand_1_out);
  and and_10 (and_10_out, buffer_4_out, nand_2_out, nor_1_out);
  and and_11 (and_11_out, buffer_9_out, nand_3_out, nor_1_out, nor_2_out);
  and and_12 (and_12_out, buffer_11_out, nand_4_out, nor_1_out, nor_2_out, nor_3_out);
  and and_13 (and_13_out, nor_1_out, nor_2_out, nor_3_out, nor_4_out, buffer_5_out);
  and and_14 (and_14_out, nor_1_out, nor_2_out, nor_3_out, nor_4_out, buffer_6_out);
  and and_15 (and_15_out, buffer_6_out, nor_4_out, nor_3_out, nor_2_out, nor_1_out);
  and and_16 (and_16_out, buffer_7_out, nor_4_out, nor_2_out, nor_3_out, nor_1_out);
  and and_17 (and_17_out, nor_3_out, nor_2_out, nor_1_out, nand_4_out, buffer_10_out);
  and and_18 (and_18_out, nor_2_out, nor_1_out, nand_3_out, buffer_8_out);
  and and_19 (and_19_out, nor_1_out, nand_2_out, buffer_3_out);
  and and_20 (and_20_out, nand_1_out, buffer_1_out);
  and and_21 (Qa_b, ~and_9_out, ~and_10_out, ~and_11_out, ~and_12_out, ~and_13_out, ~and_14_out);  // AND_Gate
  and and_22 (Qa_b_2, nor_1_out, nor_2_out, buffer_6_out, nor_3_out, nor_4_out);
  and and_23 (Qa_b_3, ~and_15_out, ~and_16_out, ~and_17_out, ~and_18_out, ~and_19_out, ~and_20_out);  // AND_Gate
endmodule

module _74688 (
  input  [7:0] P,
  input  [7:0] Q,
  input  nE,
  output P_Q
);

  wire not_1_out;
  wire [7:0] xnor_1_out;

  assign xnor_1_out = ~(~P ^ ~Q);  // XNOR_Gate xnor_1, 8 bits wide
  not not_1 (not_1_out, nE);
  nand nand_1 (P_Q, xnor_1_out[0], xnor_1_out[1], xnor_1_out[2], xnor_1_out[3], xnor_1_out[4], xnor_1_out[5], xnor_1_out[6], xnor_1_out[7], not_1_out);
endmodule
