// Logisim project L8.circ as structural Verilog: 4 circuits, main circuit main
module main (
  input  [7:0] in_1,
  input  in_2
);

  wire ALU_a_b, ALU_cn_4, carry, clock, ctrl_1_clear_flags, ctrl_1_cn, ctrl_1_m, ctrl_1_sel_ip, ctrl_1_yrw,
       multiplexer_1_out, multiplexer_2_out, nand_1_out, not_1_out, not_2_out, not_3_out, not_4_out,
       not_5_out, not_6_out, not_7_out, not_8_out, not_9_out, OUT, WF, WIR, WM, WMAR, WMBR, WR, zero;
  wire [1:0] ctrl_1_muxa, multiplexer_3_out, multiplexer_4_out, X, Y;
  wire [1:1] n74688_1_p_q;
  wire [2:0] ctrl_1_state;
  wire [3:0] ctrl_1_fn_sel, IR;
  wire [5:0] ctrl_1_mar;
  wire [7:0] ALU_f, controlled_buffer_1_out, INPUT_q, MAR_q, MBR_q, multiplexer_5_out, Output_q, reg_1_qa,
       reg_1_qb;
  wire [7:7] register_1_q;
  wire [31:0] reg_1_test;

  Clock clock_1 (.out(clock));
  Register MAR (.D(reg_1_qa), .Q(MAR_q), .clk(WMAR));  // open: en, clr
  not not_1 (not_1_out, multiplexer_2_out);
  Register INPUT (.D(in_1), .Q(INPUT_q), .clk(in_2));  // open: en, clr
  assign controlled_buffer_1_out = not_1_out ? INPUT_q : 8'bz;  // Controlled_Buffer controlled_buffer_1
  // Probe on ctrl_1_state
  ctrl ctrl_1 (
    .clock(clock), .IR(IR), .X(X), .y(Y), .zero(zero), .carry(carry), .state(ctrl_1_state),
    .MAR(ctrl_1_mar[0]), .SEL_IP(ctrl_1_sel_ip), .IR_2(ctrl_1_mar[2]), .MBR(ctrl_1_mar[1]),
    .WR(ctrl_1_mar[3]), .WM(ctrl_1_mar[4]), .MUXa(ctrl_1_muxa[0]), .MUXb(ctrl_1_muxa[1]), .YRW(ctrl_1_yrw),
    .FN_SEL(ctrl_1_fn_sel), .m(ctrl_1_m), .cn(ctrl_1_cn), .set_flags(ctrl_1_mar[5]),
    .clear_flags(ctrl_1_clear_flags));
  _74688 u_74688_1 (.P(8'hfe), .Q({MAR_q[7:1], 1'b0}), .nE(1'b0), .P_Q(n74688_1_p_q[1]));
  not not_2 (not_2_out, WM);
  Multiplexer #(.select(2), .enable("false")) multiplexer_1 (
    .in0(1'b1), .in1(1'b0), .in2(1'b1), .in3(1'b1), .out(multiplexer_1_out), .sel({n74688_1_p_q[1], MAR_q[0]}));
  Multiplexer #(.select(2), .enable("false")) multiplexer_2 (
    .in0(WM), .in1(1'b1), .in2(1'b1), .in3(1'b1), .out(multiplexer_2_out), .sel({n74688_1_p_q[1], MAR_q[0]}));
  RAM #(.bus("asynch")) ram_1 (
    .addr(MAR_q), .data(controlled_buffer_1_out), .sel(multiplexer_2_out), .ld(not_2_out));  // open: clr
  not not_3 (not_3_out, WM);
  // Probe on Y
  Register u_IR (.D(controlled_buffer_1_out), .Q({IR, X, Y}), .clk(WIR));  // open: en, clr
  Register register_1 (
    .D({2'b11, ctrl_1_mar}), .Q({register_1_q[7], OUT, WF, WM, WR, WIR, WMBR, WMAR}), .clk(clock),
    .clr(not_4_out));  // open: en
  not not_4 (not_4_out, nand_1_out);
  // Probe on multiplexer_4_out
  Multiplexer #(.width(2), .enable("false")) multiplexer_3 (
    .in0(multiplexer_4_out), .in1(Y), .out(multiplexer_3_out), .sel(ctrl_1_yrw));
  Multiplexer #(.width(2), .enable("false")) multiplexer_4 (
    .in0(2'b11), .in1(X), .out(multiplexer_4_out), .sel(ctrl_1_sel_ip));
  nand nand_1 (nand_1_out, register_1_q[7], ~clock);  // NAND_Gate
  Register MBR (.D(ALU_f), .Q(MBR_q), .clk(WMBR));  // open: en, clr
  \reg  reg_1 (
    .GrA(1'b0), .RA(multiplexer_4_out), .D(MBR_q), .Gw(not_5_out), .wa(multiplexer_3_out), .GrB(1'b0),
    .RB(Y), .Qa(reg_1_qa), .Qb(reg_1_qb), .test(reg_1_test));
  not not_5 (not_5_out, WR);
  // Probe on reg_1_test
  assign controlled_buffer_1_out = not_6_out ? MBR_q : 8'bz;  // Controlled_Buffer controlled_buffer_2
  not not_6 (not_6_out, not_3_out);
  Multiplexer #(.select(2), .width(8), .enable("false")) multiplexer_5 (
    .in0(reg_1_qa), .in1(controlled_buffer_1_out), .in2(reg_1_qb), .in3(reg_1_qb), .out(multiplexer_5_out),
    .sel(ctrl_1_muxa));
  alu ALU (
    .X(multiplexer_5_out), .Y(reg_1_qb), .M(ctrl_1_m), .Cn(ctrl_1_cn), .S(ctrl_1_fn_sel), .Cn_4(ALU_cn_4),
    .A_B(ALU_a_b), .F(ALU_f));
  not not_7 (not_7_out, multiplexer_1_out);
  // Probe on controlled_buffer_1_out
  // Probe on multiplexer_5_out
  // Probe on reg_1_qb
  // Probe on ALU_f
  not not_8 (not_8_out, WF);
  Register Output (.D(MBR_q), .en(not_7_out), .Q(Output_q), .clk(WM));  // open: clr
  _74109 u_74109_1 (.J(not_9_out), .CP(not_8_out), .K(1'b1), .S(1'b1), .R(1'b1), .Q(carry));  // open: nQ
  not not_9 (not_9_out, ALU_cn_4);
  _74109 u_74109_2 (.J(ALU_a_b), .CP(not_8_out), .K(ALU_a_b), .S(1'b1), .R(1'b1), .Q(zero));  // open: nQ
  Hex_Digit_Display hex_digit_display_1 (.value(Output_q[7:4]));  // open: dp
  Hex_Digit_Display hex_digit_display_2 (.value(Output_q[3:0]));  // open: dp
endmodule

module ctrl (
  input  clock,
  input  [3:0] IR,
  input  [1:0] X,
  input  [1:0] y,
  input  zero,
  input  carry,
  output [2:0] state,
  output MAR,
  output SEL_IP,
  output IR_2,
  output MBR,
  output WR,
  output WM,
  output MUXa,
  output MUXb,
  output YRW,
  output [3:0] FN_SEL,
  output m,
  output cn,
  output set_flags,
  output clear_flags
);

  wire ADC, ADD, AND, and_1_out, and_2_out, and_3_out, and_4_out, DEC, INC, LD, MOV, multiplexer_1_out,
       multiplexer_2_out, n74154_1_y11, n74154_1_y12, n74154_1_y13, NOT, not_1_out, not_2_out, not_3_out,
       not_4_out, OR, or_1_out, SBC, STR, SUB, T0, T1, T2, T3, T6, T7, XOR;
  wire [2:2] xor_1_out;

  not not_1 (not_1_out, clock);
  Multiplexer #(.select(3), .disabled(0), .enable("false")) multiplexer_1 (
    .in0(1'b1), .in1(1'b1), .in2(1'b1), .in3(T1), .in4(1'b1), .in5(T2), .in6(T2), .in7(T1),
    .out(multiplexer_1_out), .sel({xor_1_out[2], STR, LD}));
  not not_2 (not_2_out, INC);
  _74154 u_74154_1 (
    .iE0(1'b0), .iE1(1'b0), .A0(IR[0]), .A1(IR[1]), .A2(IR[2]), .A3(IR[3]), .Y0(DEC), .Y1(ADD), .Y2(ADC),
    .Y3(SUB), .Y4(SBC), .Y5(AND), .Y6(OR), .Y7(XOR), .Y8(NOT), .Y9(INC), .Y10(MOV), .Y11(n74154_1_y11),
    .Y12(n74154_1_y12), .Y13(n74154_1_y13), .Y14(LD), .Y15(STR));
  _74163 u_74163_1 (
    .D0(1'b0), .D1(1'b0), .D2(1'b1), .D3(1'b0), .CET(1'b1), .CEP(1'b1), .PE(multiplexer_1_out), .MR(T7),
    .CP(not_1_out), .Q0(state[0]), .Q1(state[1]), .Q2(state[2]));  // open: Q3, TC
  Multiplexer #(.select(3), .disabled(0)) multiplexer_2 (
    .in0(1'b1), .in1(zero), .in2(carry), .in3(carry), .in4(1'b0), .in5(1'b0), .in6(1'b0), .in7(1'b0),
    .out(multiplexer_2_out), .sel({1'b0, y}), .en(not_2_out));
  not not_3 (not_3_out, multiplexer_2_out);
  xor xor_1 (xor_1_out[2], X[1], X[0]);
  _74138 u_74138_1 (
    .E3(1'b1), .iE2(1'b0), .iE1(1'b0), .A0(state[0]), .A1(state[1]), .A2(state[2]), .Y0(T0), .Y1(T1),
    .Y2(T2), .Y3(T3), .Y4(T6), .Y5(T7));  // open: Y6, Y7
  and and_1 (and_1_out, STR, MOV);
  Multiplexer #(.select(3), .disabled(0)) multiplexer_3 (
    .in0(1'b1), .in1(1'b1), .in2(1'b1), .in3(1'b0), .in4(1'b0), .in5(1'b1), .in6(1'b0), .in7(1'b0),
    .out(FN_SEL[3]), .sel(IR[2:0]), .en(not_4_out));
  Multiplexer #(.select(3), .disabled(0)) multiplexer_4 (
    .in0(1'b1), .in1(1'b0), .in2(1'b0), .in3(1'b1), .in4(1'b1), .in5(1'b1), .in6(1'b1), .in7(1'b1),
    .out(FN_SEL[2]), .sel(IR[2:0]), .en(not_4_out));
  Multiplexer #(.select(3), .disabled(0)) multiplexer_5 (
    .in0(1'b1), .in1(1'b0), .in2(1'b0), .in3(1'b1), .in4(1'b1), .in5(1'b0), .in6(1'b1), .in7(1'b1),
    .out(FN_SEL[1]), .sel(IR[2:0]), .en(not_4_out));
  Multiplexer #(.select(3), .disabled(0)) multiplexer_6 (
    .in0(1'b1), .in1(1'b1), .in2(1'b1), .in3(1'b0), .in4(1'b0), .in5(1'b1), .in6(1'b1), .in7(1'b0),
    .out(FN_SEL[0]), .sel(IR[2:0]), .en(not_4_out));
  not not_4 (not_4_out, or_1_out);
  or or_1 (or_1_out, IR[3], T6);
  and and_2 (and_2_out, AND, OR, XOR, NOT);
  and and_3 (and_3_out, ADC, SUB, not_3_out);
  and and_4 (and_4_out, ADD, SUB, NOT, not_3_out);
  nand nand_1 (MAR, T0, T2);
  and and_5 (SEL_IP, T0, T1);
  not not_5 (IR_2, T1);
  nand nand_2 (MBR, T0, T2, T6);
  Multiplexer #(.select(3), .enable("false")) multiplexer_7 (
    .in0(1'b0), .in1(1'b0), .in2(1'b0), .in3(STR), .in4(1'b0), .in5(1'b1), .in6(1'b1), .in7(1'b0), .out(WR),
    .sel({T7, T3, T1}));
  nor nor_1 (WM, STR, T7);
  nor nor_2 (MUXa, LD, T6);
  nor nor_3 (MUXb, and_1_out, T6);
  nor nor_4 (YRW, T7, LD);
  nor nor_5 (m, and_2_out, T6);
  and and_6 (cn, and_3_out, ~T6);  // AND_Gate
  nor nor_6 (set_flags, and_4_out, T6);

  assign clear_flags = 1'b0;

  // Other names for the same wires on the sheet: opcode[3:0] = IR
endmodule

module alu (
  input  [7:0] X,
  input  [7:0] Y,
  input  M,
  input  Cn,
  input  [3:0] S,
  output Cn_4,
  output A_B,
  output [7:0] F
);

  wire n74181_1_a_b, n74181_1_cn_4, n74181_2_a_b;

  _74181 u_74181_1 (
    .S3(S[3]), .S2(S[2]), .S1(S[1]), .S0(S[0]), .B3(Y[3]), .A3(X[3]), .B2(Y[2]), .A2(X[2]), .B1(Y[1]),
    .A1(X[1]), .B0(Y[0]), .A0(X[0]), .M(M), .Cn(Cn), .Cn_4(n74181_1_cn_4), .F3(F[3]), .F2(F[2]),
    .A_B(n74181_1_a_b), .F1(F[1]), .F0(F[0]));  // open: G, P
  _74181 u_74181_2 (
    .S3(S[3]), .S2(S[2]), .S1(S[1]), .S0(S[0]), .B3(Y[7]), .A3(X[7]), .B2(Y[6]), .A2(X[6]), .B1(Y[5]),
    .A1(X[5]), .B0(Y[4]), .A0(X[4]), .M(M), .Cn(n74181_1_cn_4), .Cn_4(Cn_4), .F3(F[7]), .F2(F[6]),
    .A_B(n74181_2_a_b), .F1(F[5]), .F0(F[4]));  // open: G, P
  and and_1 (A_B, n74181_1_a_b, n74181_2_a_b);

  // Other names for the same wires on the sheet: XL[3:0] = X[3:0]; XH[3:0] = X[7:4]; YL[3:0] = Y[3:0];
  //   YH[3:0] = Y[7:4]
endmodule

module \reg  (
  input  GrA,
  input  [1:0] RA,
  input  [7:0] D,
  input  Gw,
  input  [1:0] wa,
  input  GrB,
  input  [1:0] RB,
  output [7:0] Qa,
  output [7:0] Qb,
  output [31:0] test
);

  wire decoder_1_out0, decoder_1_out1, decoder_1_out2, decoder_1_out3, decoder_2_out0, decoder_2_out1,
       decoder_2_out2, decoder_2_out3, not_1_out, not_2_out, not_3_out, not_4_out;
  wire [7:0] register_1_q, register_3_q, register_5_q, register_7_q;

  not not_1 (not_1_out, Gw);
  Decoder #(.select(2), .disabled(0), .enable("false")) decoder_1 (
    .out0(decoder_1_out0), .out1(decoder_1_out1), .out2(decoder_1_out2), .out3(decoder_1_out3), .sel(wa));
  not not_2 (not_2_out, Gw);
  Decoder #(.select(2), .disabled(0), .enable("false")) decoder_2 (
    .out0(decoder_2_out0), .out1(decoder_2_out1), .out2(decoder_2_out2), .out3(decoder_2_out3), .sel(wa));
  Register #(.trigger("high")) register_1 (.D(D), .en(not_1_out), .Q(register_1_q), .clk(decoder_1_out0));  // open: clr
  Register #(.trigger("high")) register_2 (.D(D), .en(not_2_out), .Q(test[7:0]), .clk(decoder_2_out0));  // open: clr
  Register #(.trigger("high")) register_3 (.D(D), .en(not_1_out), .Q(register_3_q), .clk(decoder_1_out1));  // open: clr
  Register #(.trigger("high")) register_4 (.D(D), .en(not_2_out), .Q(test[15:8]), .clk(decoder_2_out1));  // open: clr
  Register #(.trigger("high")) register_5 (.D(D), .en(not_1_out), .Q(register_5_q), .clk(decoder_1_out2));  // open: clr
  Register #(.trigger("high")) register_6 (.D(D), .en(not_2_out), .Q(test[23:16]), .clk(decoder_2_out2));  // open: clr
  not not_3 (not_3_out, GrA);
  Multiplexer #(.select(2), .width(8)) multiplexer_1 (
    .in0(register_1_q), .in1(register_3_q), .in2(register_5_q), .in3(register_7_q), .out(Qa), .sel(RA),
    .en(not_3_out));
  Register #(.trigger("high")) register_7 (.D(D), .en(not_1_out), .Q(register_7_q), .clk(decoder_1_out3));  // open: clr
  not not_4 (not_4_out, GrB);
  Multiplexer #(.select(2), .width(8)) multiplexer_2 (
    .in0(test[7:0]), .in1(test[15:8]), .in2(test[23:16]), .in3(test[31:24]), .out(Qb), .sel(RB),
    .en(not_4_out));
  Register #(.trigger("high")) register_8 (.D(D), .en(not_2_out), .Q(test[31:24]), .clk(decoder_2_out3));  // open: clr

  // Notes on the sheet:
  //   4 74670's
endmodule
