// Logisim project L8r.circ as structural Verilog: 5 circuits, main circuit main
module main (
  input  [7:0] in_1,
  input  in_2
);

  wire and_1_out, clock_1_out, ctrl_1_cn, ctrl_1_ir_2, ctrl_1_m, ctrl_1_mar, ctrl_1_mbr, ctrl_1_pc,
       ctrl_1_pc_load, ctrl_1_pc_reg, ctrl_1_sel_mem, ctrl_1_sel_x_or_y, ctrl_1_write_mem, multiplexer_2_out,
       multiplexer_3_out, multiplexer_4_out, multiplexer_5_out, n74138_1_y0, n74138_1_y1, n74138_1_y2,
       n74138_1_y3, n74138_1_y4, n74138_1_y5, n74138_1_y6, n74138_1_y7, not_1_out, not_2_out, not_3_out,
       not_4_out, not_5_out, not_6_out, not_7_out, not_8_out, not_9_out, not_10_out, not_11_out, not_12_out,
       not_13_out, not_14_out, not_15_out, not_16_out, r0, r1, r2, r3;
  wire [1:0] ctrl_1_state, IR_q_2, IR_q_3;
  wire [1:1] n74688_1_p_q;
  wire [3:0] ctrl_1_fn_sel, IR_q;
  wire [7:0] alu_1_f, controlled_buffer_1_out, INPUT_q, MAR_q, multiplexer_1_out, Output_q, pc_1_output,
       r0_q, r1_q, r2_q, r3_q, ram_1_data, Y_q;

  Clock clock_1 (.out(clock_1_out));
  // Probe on ctrl_1_state
  ctrl ctrl_1 (
    .clock(clock_1_out), .IR(IR_q), .X(IR_q_3), .y(IR_q_2), .state(ctrl_1_state), .pc(ctrl_1_pc),
    .mar(ctrl_1_mar), .ir_2(ctrl_1_ir_2), .mbr(ctrl_1_mbr), .pc_reg(ctrl_1_pc_reg), .pc_load(ctrl_1_pc_load),
    .sel_x_or_y(ctrl_1_sel_x_or_y), .sel_mem(ctrl_1_sel_mem), .write_mem(ctrl_1_write_mem), .R0(r0), .R1(r1),
    .R2(r2), .R3(r3), .FN_SEL(ctrl_1_fn_sel), .m(ctrl_1_m), .cn(ctrl_1_cn));  // open: zero, carry
  // Probe on pc_1_output
  pc pc_1 (
    .data(controlled_buffer_1_out), .enable(ctrl_1_pc), .clock(clock_1_out), .load_enable(ctrl_1_pc_load),
    .\output (pc_1_output));
  Multiplexer #(.width(8), .enable("false")) multiplexer_1 (
    .in0(pc_1_output), .in1(controlled_buffer_1_out), .out(multiplexer_1_out), .sel(ctrl_1_pc_reg));
  Register MAR (.D(multiplexer_1_out), .en(not_1_out), .Q(MAR_q), .clk(clock_1_out));  // open: clr
  not not_1 (not_1_out, ctrl_1_mar);
  not not_2 (not_2_out, ctrl_1_write_mem);
  _74688 u_74688_1 (.P(8'hfe), .Q({MAR_q[7:1], 1'b0}), .nE(1'b0), .P_Q(n74688_1_p_q[1]));
  Multiplexer #(.select(2), .enable("false")) multiplexer_2 (
    .in0(1'b1), .in1(1'b0), .in2(1'b1), .in3(1'b1), .out(multiplexer_2_out), .sel({n74688_1_p_q[1], MAR_q[0]}));
  Multiplexer #(.select(2), .enable("false")) multiplexer_3 (
    .in0(not_2_out), .in1(1'b1), .in2(1'b1), .in3(1'b1), .out(multiplexer_3_out),
    .sel({n74688_1_p_q[1], MAR_q[0]}));
  Multiplexer #(.enable("false")) multiplexer_4 (
    .in0(IR_q_2[0]), .in1(IR_q_3[0]), .out(multiplexer_4_out), .sel(ctrl_1_sel_x_or_y));
  Multiplexer #(.enable("false")) multiplexer_5 (
    .in0(IR_q_2[1]), .in1(IR_q_3[1]), .out(multiplexer_5_out), .sel(ctrl_1_sel_x_or_y));
  // Probe on ram_1_data
  RAM #(.bus("asynch")) ram_1 (
    .addr(MAR_q), .data(ram_1_data), .sel(multiplexer_3_out), .ld(ctrl_1_write_mem));  // open: clr
  not not_3 (not_3_out, ctrl_1_ir_2);
  _74138 u_74138_1 (
    .E3(1'b1), .iE2(1'b0), .iE1(1'b0), .A0(multiplexer_4_out), .A1(multiplexer_5_out), .A2(ctrl_1_sel_mem),
    .Y0(n74138_1_y0), .Y1(n74138_1_y1), .Y2(n74138_1_y2), .Y3(n74138_1_y3), .Y4(n74138_1_y4),
    .Y5(n74138_1_y5), .Y6(n74138_1_y6), .Y7(n74138_1_y7));
  Register IR (.D(ram_1_data), .en(not_3_out), .Q({IR_q, IR_q_3, IR_q_2}), .clk(clock_1_out));  // open: clr
  and and_1 (and_1_out, n74138_1_y4, n74138_1_y5, n74138_1_y6, n74138_1_y7);
  Register u_r0 (.D(alu_1_f), .en(not_4_out), .Q(r0_q), .clk(clock_1_out));  // open: clr
  not not_4 (not_4_out, r0);
  not not_5 (not_5_out, n74138_1_y0);
  Register u_r1 (.D(alu_1_f), .en(not_6_out), .Q(r1_q), .clk(clock_1_out));  // open: clr
  not not_6 (not_6_out, r1);
  not not_7 (not_7_out, n74138_1_y1);
  Register u_r2 (.D(alu_1_f), .en(not_8_out), .Q(r2_q), .clk(clock_1_out));  // open: clr
  not not_8 (not_8_out, r2);
  not not_9 (not_9_out, n74138_1_y2);
  Register u_r3 (.D(alu_1_f), .en(not_10_out), .Q(r3_q), .clk(clock_1_out));  // open: clr
  not not_10 (not_10_out, r3);
  not not_11 (not_11_out, n74138_1_y3);
  assign controlled_buffer_1_out = not_12_out ? ram_1_data : 8'bz;  // Controlled_Buffer controlled_buffer_1
  not not_12 (not_12_out, and_1_out);
  Register Y (.D(alu_1_f), .en(not_13_out), .Q(Y_q), .clk(clock_1_out));  // open: clr
  not not_13 (not_13_out, ctrl_1_mbr);
  assign controlled_buffer_1_out = not_5_out ? r0_q : 8'bz;  // Controlled_Buffer controlled_buffer_2
  assign controlled_buffer_1_out = not_7_out ? r1_q : 8'bz;  // Controlled_Buffer controlled_buffer_3
  assign controlled_buffer_1_out = not_9_out ? r2_q : 8'bz;  // Controlled_Buffer controlled_buffer_4
  assign controlled_buffer_1_out = not_11_out ? r3_q : 8'bz;  // Controlled_Buffer controlled_buffer_5
  // Probe on controlled_buffer_1_out
  assign ram_1_data = not_14_out ? controlled_buffer_1_out : 8'bz;  // Controlled_Buffer controlled_buffer_6
  not not_14 (not_14_out, ctrl_1_write_mem);
  alu alu_1 (
    .X(controlled_buffer_1_out), .Y(Y_q), .M(ctrl_1_m), .Cn(ctrl_1_cn), .S(ctrl_1_fn_sel), .F(alu_1_f));  // open: Cn_4, A_B
  Register Output (.D(ram_1_data), .en(not_15_out), .Q(Output_q), .clk(clock_1_out));  // open: clr
  not not_15 (not_15_out, multiplexer_2_out);
  Hex_Digit_Display hex_digit_display_1 (.value(Output_q[7:4]));  // open: dp
  Hex_Digit_Display hex_digit_display_2 (.value(Output_q[3:0]));  // open: dp
  not not_16 (not_16_out, multiplexer_3_out);
  Register INPUT (.D(in_1), .Q(INPUT_q), .clk(in_2));  // open: en, clr
  assign ram_1_data = not_16_out ? INPUT_q : 8'bz;  // Controlled_Buffer controlled_buffer_7
endmodule

module alu (
  input  [7:0] X,
  input  [7:0] Y,
  input  M,
  input  Cn,
  input  [3:0] S,
  output Cn_4,
  output A_B,
  output [7:0] F
);

  wire n74181_1_a_b, n74181_1_cn_4, n74181_2_a_b;

  _74181 u_74181_1 (
    .S3(S[3]), .S2(S[2]), .S1(S[1]), .S0(S[0]), .B3(Y[3]), .A3(X[3]), .B2(Y[2]), .A2(X[2]), .B1(Y[1]),
    .A1(X[1]), .B0(Y[0]), .A0(X[0]), .M(M), .Cn(Cn), .Cn_4(n74181_1_cn_4), .F3(F[3]), .F2(F[2]),
    .A_B(n74181_1_a_b), .F1(F[1]), .F0(F[0]));  // open: G, P
  _74181 u_74181_2 (
    .S3(S[3]), .S2(S[2]), .S1(S[1]), .S0(S[0]), .B3(Y[7]), .A3(X[7]), .B2(Y[6]), .A2(X[6]), .B1(Y[5]),
    .A1(X[5]), .B0(Y[4]), .A0(X[4]), .M(M), .Cn(n74181_1_cn_4), .Cn_4(Cn_4), .F3(F[7]), .F2(F[6]),
    .A_B(n74181_2_a_b), .F1(F[5]), .F0(F[4]));  // open: G, P
  and and_1 (A_B, n74181_1_a_b, n74181_2_a_b);

  // Other names for the same wires on the sheet: XL[3:0] = X[3:0]; XH[3:0] = X[7:4]; YL[3:0] = Y[3:0];
  //   YH[3:0] = Y[7:4]
endmodule

module \reg  (
  input  GrA,
  input  [1:0] RA,
  input  [7:0] D,
  input  Gw,
  input  [1:0] wa,
  output [7:0] Qa
);

  wire decoder_1_out0, decoder_1_out1, decoder_1_out2, decoder_1_out3, not_1_out, not_2_out;
  wire [7:0] register_1_q, register_2_q, register_3_q, register_4_q;

  not not_1 (not_1_out, Gw);
  Decoder #(.select(2), .disabled(0), .enable("false")) decoder_1 (
    .out0(decoder_1_out0), .out1(decoder_1_out1), .out2(decoder_1_out2), .out3(decoder_1_out3), .sel(wa));
  Register #(.trigger("high")) register_1 (.D(D), .en(not_1_out), .Q(register_1_q), .clk(decoder_1_out0));  // open: clr
  Register #(.trigger("high")) register_2 (.D(D), .en(not_1_out), .Q(register_2_q), .clk(decoder_1_out1));  // open: clr
  Register #(.trigger("high")) register_3 (.D(D), .en(not_1_out), .Q(register_3_q), .clk(decoder_1_out2));  // open: clr
  not not_2 (not_2_out, GrA);
  Multiplexer #(.select(2), .width(8)) multiplexer_1 (
    .in0(register_1_q), .in1(register_2_q), .in2(register_3_q), .in3(register_4_q), .out(Qa), .sel(RA),
    .en(not_2_out));
  Register #(.trigger("high")) register_4 (.D(D), .en(not_1_out), .Q(register_4_q), .clk(decoder_1_out3));  // open: clr

  // Notes on the sheet:
  //   2 74670's
endmodule

module pc (
  input  [7:0] data,
  input  enable,
  input  clock,
  input  load_enable,
  output [7:0] \output 
);

  wire n74161_1_tc;

  _74161 u_74161_1 (
    .D0(data[0]), .D1(data[1]), .D2(data[2]), .D3(data[3]), .CET(enable), .CEP(enable), .PE(load_enable),
    .MR(1'b1), .CP(clock), .Q0(\output [0]), .Q1(\output [1]), .Q2(\output [2]), .Q3(\output [3]),
    .TC(n74161_1_tc));
  _74161 u_74161_2 (
    .D0(data[4]), .D1(data[5]), .D2(data[6]), .D3(data[7]), .CET(n74161_1_tc), .CEP(n74161_1_tc),
    .PE(load_enable), .MR(1'b1), .CP(clock), .Q0(\output [4]), .Q1(\output [5]), .Q2(\output [6]),
    .Q3(\output [7]));  // open: TC
endmodule

module ctrl (
  input  clock,
  input  [3:0] IR,
  input  [1:0] X,
  input  [1:0] y,
  input  zero,
  input  carry,
  output pc,
  output [1:0] state,
  output mar,
  output ir_2,
  output mbr,
  output pc_reg,
  output pc_load,
  output sel_x_or_y,
  output sel_mem,
  output write_mem,
  output R0,
  output R1,
  output R2,
  output R3,
  output [3:0] FN_SEL,
  output m,
  output cn
);

  wire ADC, ADD, AND, and_1_out, and_2_out, DEC, INC, JMP, LD, LDI, n74154_1_y10, n74154_1_y11, nand_1_out,
       NOT, not_1_out, not_2_out, OR, or_1_out, SBC, STR, SUB, T0, T3, XOR;

  not not_1 (not_1_out, clock);
  _74154 u_74154_1 (
    .iE0(1'b0), .iE1(1'b0), .A0(IR[0]), .A1(IR[1]), .A2(IR[2]), .A3(IR[3]), .Y0(DEC), .Y1(ADD), .Y2(ADC),
    .Y3(SUB), .Y4(SBC), .Y5(AND), .Y6(OR), .Y7(XOR), .Y8(NOT), .Y9(INC), .Y10(n74154_1_y10),
    .Y11(n74154_1_y11), .Y12(JMP), .Y13(LDI), .Y14(LD), .Y15(STR));
  _74163 u_74163_1 (
    .D0(1'b1), .D1(1'b0), .D2(1'b0), .D3(1'b0), .CET(1'b1), .CEP(1'b1), .PE(1'b1), .MR(1'b1), .CP(not_1_out),
    .Q0(state[0]), .Q1(state[1]));  // open: Q2, Q3, TC
  _74138 u_74138_1 (
    .E3(1'b1), .iE2(1'b0), .iE1(1'b0), .A0(state[0]), .A1(state[1]), .A2(1'b0), .Y0(T0), .Y1(ir_2), .Y2(mbr),
    .Y3(T3));  // open: Y4, Y5, Y6, Y7
  Multiplexer #(.select(3), .disabled(0)) multiplexer_1 (
    .in0(1'b1), .in1(1'b1), .in2(1'b1), .in3(1'b0), .in4(1'b0), .in5(1'b1), .in6(1'b0), .in7(1'b0),
    .out(FN_SEL[3]), .sel(IR[2:0]), .en(not_2_out));
  Multiplexer #(.select(3), .disabled(0)) multiplexer_2 (
    .in0(1'b1), .in1(1'b0), .in2(1'b0), .in3(1'b1), .in4(1'b1), .in5(1'b1), .in6(1'b1), .in7(1'b1),
    .out(FN_SEL[2]), .sel(IR[2:0]), .en(not_2_out));
  Multiplexer #(.select(3), .disabled(0)) multiplexer_3 (
    .in0(1'b1), .in1(1'b0), .in2(1'b0), .in3(1'b1), .in4(1'b1), .in5(1'b0), .in6(1'b1), .in7(1'b1),
    .out(FN_SEL[1]), .sel(IR[2:0]), .en(not_2_out));
  Multiplexer #(.select(3), .disabled(0)) multiplexer_4 (
    .in0(1'b1), .in1(1'b1), .in2(1'b1), .in3(1'b0), .in4(1'b0), .in5(1'b1), .in6(1'b1), .in7(1'b0),
    .out(FN_SEL[0]), .sel(IR[2:0]), .en(not_2_out));
  not not_2 (not_2_out, or_1_out);
  or or_1 (or_1_out, IR[3], T3);
  nand nand_1 (nand_1_out, LDI, JMP);
  and and_1 (and_1_out, LD, LDI);
  _74138 u_74138_2 (
    .E3(STR), .iE2(T3), .iE1(T3), .A0(X[0]), .A1(X[1]), .A2(1'b0), .Y0(R0), .Y1(R1), .Y2(R2), .Y3(R3));  // open: Y4, Y5, Y6, Y7
  and and_2 (and_2_out, AND, OR, XOR, NOT);
  Multiplexer #(.select(3), .enable("false")) multiplexer_5 (
    .in0(1'b1), .in1(1'b1), .in2(1'b1), .in3(T3), .in4(1'b1), .in5(T3), .in6(T3), .in7(1'b1), .out(cn),
    .sel({INC, SUB, ADC}));
  Multiplexer #(.select(2), .enable("false")) multiplexer_6 (
    .in0(1'b0), .in1(1'b1), .in2(1'b0), .in3(nand_1_out), .out(pc), .sel(state));
  and and_3 (mar, T0, mbr);
  Multiplexer #(.select(2), .enable("false")) multiplexer_7 (
    .in0(1'b0), .in1(1'b1), .in2(LDI), .in3(1'b1), .out(pc_reg), .sel(state));
  or or_2 (pc_load, JMP, T3);
  nor nor_1 (sel_mem, T3, and_1_out);
  or or_3 (write_mem, T3, STR);
  nor nor_2 (m, and_2_out, T3);

  assign sel_x_or_y = mbr;

  // Other names for the same wires on the sheet: opcode[3:0] = IR; T1 = ir_2; T2 = mbr
endmodule
